# Fritzing sketch 18b20_esp8266_example (saved by Fritzing 0.9.3b)

parts:
  Componente1 = NodeMcu base board
  Part1 = KY-001 Temperature Sensor Module [package="Breakout board"]

nets:
  N1: Componente1.D0, Part1.S
  N2: Componente1.3V, Part1.Vin
  N3: Componente1.GND, Part1.-

custom parts:
  NodeMcu base board: This is the based board shield for NodeMCU (Lolin)
  KY-001 Temperature Sensor Module: Arduino Temperature Sensor Module Keyes KY-001, Allows ambient temperature measurement using digital serial bus (DS18B20)
