# Fritzing sketch 18b20_example (saved by Fritzing 0.9.3b)
breadboards: 1

parts:
  DS1 = DS18B20 1-Wire Temperature Sensor [part_number=DS18B20]
  R1 = Resistor [tolerance=±5% resistance=220 package=THT]
  Componente1 = Arduino Nano Expansion Board (Rev3.0)

nets:
  GND: DS1.GND, Componente1.GND
  N1: DS1.DQ, R1.Pin_1, Componente1.D2
  VDD: DS1.VDD, R1.Pin_0, Componente1.5V

custom parts:
  Arduino Nano Expansion Board (Rev3.0): Arduino Nano 3.0 IO expansion board
