# Fritzing sketch move_servo_iot (saved by Fritzing 0.9.3b)

parts:
  Componente2 = ESP12E Motor Shield
  R1 = Servo 360º [package=THT]

nets:
  N1: Componente2.GND, Componente2.G, R1.-
  N2: Componente2.5V, R1.+
  N3: Componente2.D4, R1.S

custom parts:
  ESP12E Motor Shield: ESP8266 WiFi Motor Drive Expansion Board For NodeMCU ESP-12E
  Servo 360º: A continuous rotation servo
