# Fritzing sketch read_temp_iot (saved by Fritzing 0.9.3b)

parts:
  Componente1 = ESP12E Motor Shield
  Hall-effect1 = DHT11 Humitidy and Temperature Sensor

nets:
  GND: Componente1.G, Componente1.GND, Hall-effect1.GND
  N1: Componente1.VU, Componente1.VUSB, Hall-effect1.VDD
  N2: Componente1.A0, Hall-effect1.S

custom parts:
  ESP12E Motor Shield: ESP8266 WiFi Motor Drive Expansion Board For NodeMCU ESP-12E
  DHT11 Humitidy and Temperature Sensor: 44E Hall-effect Sensor
