# Fritzing sketch read_temp_iot1 (saved by Fritzing 0.9.3b)

parts:
  DHT1 = DHT11 Humitidy and Temperature Sensor
  Componente2 = ESP12E Motor Shield

nets:
  N1: DHT1.VDD, Componente2.3V
  N2: DHT1.S, Componente2.D3
  GND: DHT1.GND, Componente2.GND

custom parts:
  DHT11 Humitidy and Temperature Sensor: DHT11 Humidity and Temperature Sensor
  ESP12E Motor Shield: ESP8266 WiFi Motor Drive Expansion Board For NodeMCU ESP-12E
