# Fritzing sketch read_temp_realy_iot (saved by Fritzing 0.9.3b)

parts:
  KY-1 = Keyes Relay [package=THT]
  DHT1 = DHT11 Humitidy and Temperature Sensor
  Componente2 = ESP12E Motor Shield

nets:
  N1: KY-1.signal, Componente2.D2
  N2: KY-1.power, DHT1.VDD, Componente2.3V
  GND: KY-1.ground, DHT1.GND, Componente2.GND
  N3: DHT1.S, Componente2.D3

custom parts:
  Keyes Relay: The Keyes 5V relay module is suitable for SCM development, home appliance control. It uses a 5V~12V TIL control signal which can control DC / AC signal.
  DHT11 Humitidy and Temperature Sensor: DHT11 Humidity and Temperature Sensor
  ESP12E Motor Shield: ESP8266 WiFi Motor Drive Expansion Board For NodeMCU ESP-12E
