# Fritzing sketch read_temp_relay_iot_wemosD1R32 (saved by Fritzing 0.9.3b)

parts:
  KY-1 = Keyes Relay [package=THT]
  DHT1 = DHT11 Humitidy and Temperature Sensor
  COMPUTER_FAN2 = Computer fan
  WeMos_D1_R32_Shield1 = WeMos D1 R32 with Arduino Sensor Shield v5

nets:
  N1: KY-1.signal, WeMos_D1_R32_Shield1.D2
  N2: KY-1.power, WeMos_D1_R32_Shield1.5V#45
  N3: KY-1.ground, WeMos_D1_R32_Shield1.GND#22
  N4: KY-1.C, COMPUTER_FAN2.RED
  N5: KY-1.NO, WeMos_D1_R32_Shield1.5V#58
  N6: DHT1.VDD, WeMos_D1_R32_Shield1.5V#46
  N7: DHT1.S, WeMos_D1_R32_Shield1.D3
  N8: DHT1.GND, WeMos_D1_R32_Shield1.GND#23
  N9: COMPUTER_FAN2.BLACK, WeMos_D1_R32_Shield1.GND#42

custom parts:
  Keyes Relay: The Keyes 5V relay module is suitable for SCM development, home appliance control. It uses a 5V~12V TIL control signal which can control DC / AC signal.
  DHT11 Humitidy and Temperature Sensor: DHT11 Humidity and Temperature Sensor
  Computer fan: This is a 5V computer fan
  WeMos D1 R32 with Arduino Sensor Shield v5: The D1 R32 is a mini wifi board based on the ESP32 with an Arduino Sensor Shield v5
