# Fritzing sketch temp_light_relay_iot (saved by Fritzing 0.9.3b)

parts:
  DHT1 = DHT11 Humitidy and Temperature Sensor
  Componente2 = ESP12E Motor Shield
  COMPUTER_FAN1 = Computer fan
  R1 = Photocell (LDR) [package=THT]
  L1 = LED Light [package=THT]
  L2 = LED Light Transformer [package=THT]
  Keyes_double_relay1 = Keyes Double Relay [package=THT]
  AC_PLUG1 = AC Plug
  Part2 = Terminal block

nets:
  VDD: DHT1.VDD, Componente2.3V, Keyes_double_relay1.VCC
  N1: DHT1.S, Componente2.D3
  GND: DHT1.GND, Componente2.GND#44, Componente2.GND#46, Keyes_double_relay1.GND
  N2: Componente2.D1, Keyes_double_relay1.IN1
  N3: Componente2.D2, Keyes_double_relay1.IN2
  N4: Componente2.GND#16, Componente2.G, Componente2.GND#52, R1.-, Keyes_double_relay1.C2
  N5: Componente2.VU, Componente2.VUSB, R1.+, Part2.OUT2
  N6: Componente2.A0, R1.S
  N7: COMPUTER_FAN1.RED, Part2.IN2
  N8: COMPUTER_FAN1.BLACK, Keyes_double_relay1.NO2
  N9: L1.-, L2.-
  N10: L1.+, L2.+
  N11: L2.L, Part2.OUT1
  N12: L2.N, Keyes_double_relay1.NO1
  N13: Keyes_double_relay1.C1, AC_PLUG1.BLACK
  N14: AC_PLUG1.RED, Part2.IN1

notes:
  Dupont M/F Cables
  DuPont F/F Cables
  5V Fan Cable
  0V Fan Cable
  L
  N
  +
  -
  L (Plug)
  N (Plug)
  Mini-transformer
  Computer fan
  LED Light
  AC Plug
  NodeMCU+Extension Shield
  LDR Module
  DHT11 Module

custom parts:
  DHT11 Humitidy and Temperature Sensor: DHT11 Humidity and Temperature Sensor
  ESP12E Motor Shield: ESP8266 WiFi Motor Drive Expansion Board For NodeMCU ESP-12E
  Computer fan: This is a 5V computer fan
  Photocell (LDR): A generic light dependent resistor (LDR)
  Keyes Double Relay: The Keyes 5V double relay module is suitable for SCM development, home appliance control. It uses a 5V~12V TIL control signal which can control DC / AC signal.
  AC Plug: This is a 220V/110 Vac plug
