# Fritzing sketch OLED_128x32_I2C (saved by Fritzing 0.9.3b)

parts:
  Componente1 = Arduino Nano Expansion Board (Rev3.0)
  Grove1 = Grove OLED 128x96

nets:
  GND: Componente1.GND, Grove1.GND
  5V: Componente1.5V, Grove1.VCC
  N1: Componente1.SCL, Grove1.SCL
  N2: Componente1.SDA, Grove1.SDA

custom parts:
  Arduino Nano Expansion Board (Rev3.0): Arduino Nano 3.0 IO expansion board
