# Fritzing sketch bluetooth_leds_leonardo (saved by Fritzing 0.9.3b)

parts:
  Leonardo_Shield1 = Arduino Leonardo with Arduino Sensor Shield v5
  Part1 = Semaphore module

nets:
  N1: Leonardo_Shield1.D5, Part1.G
  N2: Leonardo_Shield1.D6, Part1.Y
  N3: Leonardo_Shield1.D7, Part1.R
  GND: Leonardo_Shield1.GND, Part1.GND

custom parts:
  Arduino Leonardo with Arduino Sensor Shield v5: The D1 R32 is a mini wifi board based on the ESP32 with an Arduino Sensor Shield v5
