# Fritzing sketch bluetooth_leds_nodemcu (saved by Fritzing 0.9.3b)

parts:
  Part2 = Semaphore module
  Componente1 = NodeMcu base board

nets:
  GND: Part2.GND, Componente1.GND
  N1: Part2.G, Componente1.D5
  N2: Part2.R, Componente1.D7
  N3: Part2.Y, Componente1.D6

custom parts:
  NodeMcu base board: ESP8266 WiFi Expansion Board For NodeMCU ESP-12E
