# Fritzing sketch bmp180_nano_example (saved by Fritzing 0.9.3b)

parts:
  Componente2 = Arduino Nano Expansion Board (Rev3.0)
  Componente3 = Adafruit BMP180

nets:
  GND: Componente2.GND, Componente3.GND
  3V3: Componente2.3V3, Componente3.+3V3
  N1: Componente2.SCL, Componente3.SCL
  N2: Componente2.SDA, Componente3.SDA

custom parts:
  Arduino Nano Expansion Board (Rev3.0): Arduino Nano 3.0 IO expansion board
  Adafruit BMP180: This precision sensor from Bosch is the best low-cost sensing solution for measuring barometric pressure and temperature. Because pressure changes with altitude you can also use it as an altimeter! The sensor is soldered onto a PCB with a 3.3V regulator, I2C level shifter and pull-up resistors on the I2C pins. The BMP180 is the next-generation of sensors from Bosch, and replaces the BMP085.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
