# Fritzing sketch bmp180_wemosD1R32_example (saved by Fritzing 0.9.3b)

parts:
  Componente3 = Adafruit BMP180
  WeMos_D1_R1 = WeMos D1 R32

nets:
  +3V3: Componente3.+3V3, WeMos_D1_R1.3.3V
  GND: Componente3.GND, WeMos_D1_R1.GND
  N1: Componente3.SCL, WeMos_D1_R1.SCL
  N2: Componente3.SDA, WeMos_D1_R1.SDA

custom parts:
  Adafruit BMP180: This precision sensor from Bosch is the best low-cost sensing solution for measuring barometric pressure and temperature. Because pressure changes with altitude you can also use it as an altimeter! The sensor is soldered onto a PCB with a 3.3V regulator, I2C level shifter and pull-up resistors on the I2C pins. The BMP180 is the next-generation of sensors from Bosch, and replaces the BMP085.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
  WeMos D1 R32: The D1 R32 is a mini wifi board based on the ESP32.
