# Fritzing sketch buzzer_breadboard (saved by Fritzing 0.9.3b)
breadboards: 1

parts:
  R1 = Resistor [tolerance=±5% resistance=220 package=THT]
  Q1 = PNP-Transistor [package="TO92 [THT]"]
  Componente1 = Arduino Nano (Rev3.0)
  J1 = Piezo Speaker
  VCC1 = Battery block 9V

nets (from the schematic view):
  N1: R1.Pin_0, Componente1.D8
  N2: R1.Pin_1, Q1.B
  N3: Q1.E, Componente1.VIN, VCC1.+
  N4: Q1.C, J1.pin1
  N5: J1.pin2, VCC1.-
