# Fritzing sketch buzzer_button (saved by Fritzing 0.9.3b)
breadboards: 1

parts:
  Componente1 = Arduino Nano Expansion Board (Rev3.0)
  Part1 = KY-006 Passive Buzzer Module [package="Breakout board"]
  S1 = Pushbutton [package="[SMD]"]
  R1 = Resistor [tolerance=±5% resistance=220 package="1206 [SMD]"]

nets:
  N1: Componente1.D2, S1.Pin_3, S1.Pin_4, R1.Pin_1
  N2: Componente1.D8, Part1.S
  N3: Componente1.GND#58, Part1.-
  N4: Componente1.5V#81, R1.Pin_0
  N5: Componente1.5V#87, Part1.+5V

custom parts:
  Arduino Nano Expansion Board (Rev3.0): Arduino Nano 3.0 IO expansion board
  KY-006 Passive Buzzer Module: Passive Piezoelectric Buzzer Module Keyes KY-006, it can produce a range of sound tones depending on the input frequency.
