# Fritzing sketch buzzer_pwm (saved by Fritzing 0.9.3b)

parts:
  Parte1 = Arduino Nano (Rev3.0)
  VCC2 = Battery block 9V  # not connected
  S5 = Piezo-electric buzzer

nets:
  N1: Parte1.D3/PWM0, S5.Signal
  GND: Parte1.GND, S5.Gnd
  5V: Parte1.5V, S5.Vcc

custom parts:
  Arduino Nano (Rev3.0): Arduino Nano 3.0 IO expansion board
  Piezo-electric buzzer: Piezo-electric buzzer (speaker)
