# Fritzing sketch dht11_esp8266_example (saved by Fritzing 0.9.3b)

parts:
  Componente1 = NodeMcu base board
  DHT1 = DHT11 Humitidy and Temperature Sensor

nets:
  N1: Componente1.D0, DHT1.S
  GND: Componente1.G, Componente1.GND, DHT1.GND
  N2: Componente1.3V, DHT1.VDD

custom parts:
  NodeMcu base board: This is the based board shield for NodeMCU (Lolin)
  DHT11 Humitidy and Temperature Sensor: DHT11 Humidity and Temperature Sensor
