# Fritzing sketch dht11_example (saved by Fritzing 0.9.3b)

parts:
  J1 = male pin header, 3 pins [form="♂ (male)"]
  Componente2 = Arduino Nano Expansion Board (Rev3.0)

nets:
  N1: J1.pin1, Componente2.D2, Componente2.D3/PWM0
  N2: J1.pin2, Componente2.5V
  N3: J1.pin3, Componente2.GND

custom parts:
  Arduino Nano Expansion Board (Rev3.0): Arduino Nano 3.0 IO expansion board
