# Fritzing sketch gas_mq3 (saved by Fritzing 0.9.3b)

parts:
  Componente1 = MQ-3 breakout
  Componente2 = Arduino Nano Expansion Board (Rev3.0)

nets:
  VCC: Componente1.VCC, Componente2.5V
  N1: Componente1.GND, Componente2.GND#62
  N2: Componente1.DO, Componente2.D12, Componente2.GND#55
  N3: Componente1.AO, Componente2.A0

custom parts:
  MQ-3 breakout: Alcohol sensor is capable of detecting alcohol (ethanol) particles on itself and gives the information in digital form back to us to manipulate with it. SKU:101251 • Voltage: 5V DC • Power: max 750mW • Measurement range: 0.04-4mg/L
  Arduino Nano Expansion Board (Rev3.0): Arduino Nano 3.0 IO expansion board
