# Fritzing sketch gas_mq3_calibrated (saved by Fritzing 0.9.3b)

parts:
  Componente1 = MQ-3 breakout
  Componente2 = Arduino Nano Expansion Board (Rev3.0)
  Part1 = KY-004 Key Switch Module [package="Breakout board"]

nets:
  N1: Componente1.VCC, Componente2.5V#97
  N2: Componente1.GND, Componente2.GND#68
  N3: Componente1.AO, Componente2.A0
  N4: Componente2.D3/PWM0, Part1.S
  N5: Componente2.GND#53, Part1.-
  N6: Componente2.5V#82, Part1.Vin

custom parts:
  MQ-3 breakout: Alcohol sensor is capable of detecting alcohol (ethanol) particles on itself and gives the information in digital form back to us to manipulate with it. SKU:101251 • Voltage: 5V DC • Power: max 750mW • Measurement range: 0.04-4mg/L
  Arduino Nano Expansion Board (Rev3.0): Arduino Nano 3.0 IO expansion board
  KY-004 Key Switch Module: Arduino Key Switch Module Keyes KY-004 is a push button that will output a high signal when pressed.
