# Fritzing sketch gas_mq3_calibrated_leonardo (saved by Fritzing 0.9.3b)

parts:
  Leonardo_Shield2 = Arduino Leonardo with Arduino Sensor Shield v5
  Componente2 = MQ-3 breakout
  Part3 = KY-004 Key Switch Module [package="Breakout board"]

nets:
  N1: Leonardo_Shield2.D3, Part3.S
  N2: Leonardo_Shield2.D12, Componente2.DO
  N3: Leonardo_Shield2.GND#23, Part3.-
  N4: Leonardo_Shield2.A0, Componente2.AO
  N5: Leonardo_Shield2.GND#65, Componente2.GND
  5V: Leonardo_Shield2.5V, Componente2.VCC

custom parts:
  Arduino Leonardo with Arduino Sensor Shield v5: The D1 R32 is a mini wifi board based on the ESP32 with an Arduino Sensor Shield v5
  MQ-3 breakout: Alcohol sensor is capable of detecting alcohol (ethanol) particles on itself and gives the information in digital form back to us to manipulate with it. SKU:101251 • Voltage: 5V DC • Power: max 750mW • Measurement range: 0.04-4mg/L
  KY-004 Key Switch Module: Arduino Key Switch Module Keyes KY-004 is a push button that will output a high signal when pressed.
