# Fritzing sketch gas_mq3_calibrated_nano (saved by Fritzing 0.9.3b)

parts:
  Componente1 = MQ-3 breakout
  Componente3 = Arduino Nano (Rev3.0)
  Part2 = KY-004 Key Switch Module [package="Breakout board"]

nets:
  N1: Componente1.VCC, Componente3.5V#83
  N2: Componente1.GND, Componente3.GND#54
  N3: Componente1.DO, Componente3.D11/PWM5
  N4: Componente1.AO, Componente3.A0
  N5: Componente3.D3/PWM0, Part2.S
  N6: Componente3.GND#62, Part2.-
  N7: Componente3.5V#91, Part2.Vin

custom parts:
  MQ-3 breakout: Alcohol sensor is capable of detecting alcohol (ethanol) particles on itself and gives the information in digital form back to us to manipulate with it. SKU:101251 • Voltage: 5V DC • Power: max 750mW • Measurement range: 0.04-4mg/L
  Arduino Nano (Rev3.0): Arduino Nano 3.0 IO expansion board
  KY-004 Key Switch Module: Arduino Key Switch Module Keyes KY-004 is a push button that will output a high signal when pressed.
