# Fritzing sketch gas_mq3_calibrated_nodemcu (saved by Fritzing 0.9.3b)

parts:
  Componente1 = MQ-3 breakout
  Componente4 = NodeMcu base board
  Part5 = KY-004 Key Switch Module [package="Breakout board"]

nets:
  VCC: Componente1.VCC, Componente4.3V, Part5.Vin
  GND: Componente1.GND, Componente4.GND, Part5.-
  N1: Componente1.DO, Componente4.D2
  N2: Componente1.AO, Componente4.A0
  N3: Componente4.D3, Part5.S

custom parts:
  MQ-3 breakout: Alcohol sensor is capable of detecting alcohol (ethanol) particles on itself and gives the information in digital form back to us to manipulate with it. SKU:101251 • Voltage: 5V DC • Power: max 750mW • Measurement range: 0.04-4mg/L
  NodeMcu base board: ESP8266 WiFi Expansion Board For NodeMCU ESP-12E
  KY-004 Key Switch Module: Arduino Key Switch Module Keyes KY-004 is a push button that will output a high signal when pressed.
