# Fritzing sketch gas_mq3_calibrated_wemosD1R32 (saved by Fritzing 0.9.3b)

parts:
  Componente1 = MQ-3 breakout
  WeMos_D1_R32_Shield1 = WeMos D1 R32 with Arduino Sensor Shield v5
  Part4 = KY-004 Key Switch Module [package="Breakout board"]

nets:
  N1: Componente1.VCC, WeMos_D1_R32_Shield1.5V#55
  N2: Componente1.GND, WeMos_D1_R32_Shield1.GND#33
  N3: Componente1.DO, WeMos_D1_R32_Shield1.D12
  N4: Componente1.AO, WeMos_D1_R32_Shield1.A0
  N5: WeMos_D1_R32_Shield1.D3, Part4.S
  N6: WeMos_D1_R32_Shield1.GND#23, Part4.-
  N7: WeMos_D1_R32_Shield1.5V#46, Part4.Vin

custom parts:
  MQ-3 breakout: Alcohol sensor is capable of detecting alcohol (ethanol) particles on itself and gives the information in digital form back to us to manipulate with it. SKU:101251 • Voltage: 5V DC • Power: max 750mW • Measurement range: 0.04-4mg/L
  WeMos D1 R32 with Arduino Sensor Shield v5: The D1 R32 is a mini wifi board based on the ESP32 with an Arduino Sensor Shield v5
  KY-004 Key Switch Module: Arduino Key Switch Module Keyes KY-004 is a push button that will output a high signal when pressed.
