# Fritzing sketch gas_mq3_leonardo (saved by Fritzing 0.9.3b)

parts:
  Leonardo_Shield2 = Arduino Leonardo with Arduino Sensor Shield v5
  Componente2 = MQ-3 breakout

nets:
  N1: Leonardo_Shield2.D12, Componente2.DO
  N2: Leonardo_Shield2.A0, Componente2.AO
  GND: Leonardo_Shield2.GND, Componente2.GND
  5V: Leonardo_Shield2.5V, Componente2.VCC

custom parts:
  Arduino Leonardo with Arduino Sensor Shield v5: The D1 R32 is a mini wifi board based on the ESP32 with an Arduino Sensor Shield v5
  MQ-3 breakout: Alcohol sensor is capable of detecting alcohol (ethanol) particles on itself and gives the information in digital form back to us to manipulate with it. SKU:101251 • Voltage: 5V DC • Power: max 750mW • Measurement range: 0.04-4mg/L
