# Fritzing sketch gas_mq3_nano (saved by Fritzing 0.9.3b)

parts:
  Componente1 = MQ-3 breakout
  Componente3 = Arduino Nano (Rev3.0)

nets:
  VCC: Componente1.VCC, Componente3.5V
  GND: Componente1.GND, Componente3.GND
  N1: Componente1.DO, Componente3.D11/PWM5
  N2: Componente1.AO, Componente3.A0

custom parts:
  MQ-3 breakout: Alcohol sensor is capable of detecting alcohol (ethanol) particles on itself and gives the information in digital form back to us to manipulate with it. SKU:101251 • Voltage: 5V DC • Power: max 750mW • Measurement range: 0.04-4mg/L
  Arduino Nano (Rev3.0): Arduino Nano 3.0 IO expansion board
