# Fritzing sketch gas_mq3_nodemcu (saved by Fritzing 0.9.3b)

parts:
  Componente1 = MQ-3 breakout
  Componente4 = NodeMcu base board

nets:
  N1: Componente1.VCC, Componente4.3V
  GND: Componente1.GND, Componente4.GND
  N2: Componente1.DO, Componente4.D2
  N3: Componente1.AO, Componente4.A0

custom parts:
  MQ-3 breakout: Alcohol sensor is capable of detecting alcohol (ethanol) particles on itself and gives the information in digital form back to us to manipulate with it. SKU:101251 • Voltage: 5V DC • Power: max 750mW • Measurement range: 0.04-4mg/L
  NodeMcu base board: ESP8266 WiFi Expansion Board For NodeMCU ESP-12E
