# Fritzing sketch gas_mq3_wemosD1R32 (saved by Fritzing 0.9.3b)

parts:
  Componente1 = MQ-3 breakout
  WeMos_D1_R32_Shield1 = WeMos D1 R32 with Arduino Sensor Shield v5

nets:
  VCC: Componente1.VCC, WeMos_D1_R32_Shield1.5V
  GND: Componente1.GND, WeMos_D1_R32_Shield1.GND
  N1: Componente1.DO, WeMos_D1_R32_Shield1.D12
  N2: Componente1.AO, WeMos_D1_R32_Shield1.A0

custom parts:
  MQ-3 breakout: Alcohol sensor is capable of detecting alcohol (ethanol) particles on itself and gives the information in digital form back to us to manipulate with it. SKU:101251 • Voltage: 5V DC • Power: max 750mW • Measurement range: 0.04-4mg/L
  WeMos D1 R32 with Arduino Sensor Shield v5: The D1 R32 is a mini wifi board based on the ESP32 with an Arduino Sensor Shield v5
