# Fritzing sketch joystick_example (saved by Fritzing 0.9.3b)

parts:
  Componente1 = Arduino Nano Expansion Board (Rev3.0)
  U1 = JOYSTICK-PSP1000 [package=joystick-psp1000]

nets:
  N1: Componente1.A1, U1.Y
  N2: Componente1.A0, U1.X
  GND: Componente1.GND, U1.GND
  5V: Componente1.5V, U1.VCC

custom parts:
  Arduino Nano Expansion Board (Rev3.0): Arduino Nano 3.0 IO expansion board
