# Fritzing sketch lcd_display (saved by Fritzing 0.9.3b)
breadboards: 1

parts:
  VCC2 = Battery block 9V
  LCD1 = LCD screen
  Componente1 = Arduino Nano (Rev3.0) (ICSP)
  R2 = Trimmer Potentiometer [maximum_resistance=10kΩ package=THT]  # not connected
  R3 = Resistor [tolerance=±5% resistance=220 package=THT]

nets:
  N1: VCC2.-, Componente1.GND
  N2: VCC2.+, Componente1.VIN
  N3: LCD1.VSS, LCD1.R/W, LCD1.LED-
  N4: LCD1.VDD, R3.Pin_0
  N5: LCD1.RS, Componente1.D11/MOSI
  N6: LCD1.E, Componente1.D12/MISO
  N7: LCD1.DB4, Componente1.D3
  N8: LCD1.DB5, Componente1.D4
  N9: LCD1.DB6, Componente1.D5
  N10: LCD1.DB7, Componente1.D6
  N11: LCD1.LED+, R3.Pin_1
