# Fritzing sketch lcd_example (saved by Fritzing 0.9.3b)

parts:
  Componente1 = Arduino Nano Expansion Board (Rev3.0)
  LCD1 = LCD screen

nets:
  N1: Componente1.D3/PWM0, LCD1.DB4
  N2: Componente1.D4, LCD1.DB5
  N3: Componente1.D5/PWM1, LCD1.DB6
  N4: Componente1.D6/PWM2, LCD1.DB7
  N5: Componente1.D11/PWM5, LCD1.RS
  N6: Componente1.D12, LCD1.E
  N7: Componente1.GND#66, LCD1.VSS
  N8: Componente1.GND#76, LCD1.V0
  5V: Componente1.5V, LCD1.VDD

custom parts:
  Arduino Nano Expansion Board (Rev3.0): Arduino Nano 3.0 IO expansion board
