# Fritzing sketch lcd_example1 (saved by Fritzing 0.9.3b)
breadboards: 1

parts:
  Componente1 = Arduino Nano Expansion Board (Rev3.0)
  LCD1 = LCD screen
  S3 = Pushbutton [package="[THT]"]
  R5 = Resistor [tolerance=±5% resistance=220 package="2512 [SMD]"]

nets:
  N1: Componente1.D2, S3.Pin_3, S3.Pin_4, R5.Pin_1
  N2: Componente1.D3/PWM0, LCD1.DB4
  N3: Componente1.D4, LCD1.DB5
  N4: Componente1.D5/PWM1, LCD1.DB6
  N5: Componente1.D6/PWM2, LCD1.DB7
  N6: Componente1.D11/PWM5, LCD1.RS
  N7: Componente1.D12, LCD1.E
  N8: Componente1.GND#52, S3.Pin_1, S3.Pin_2
  N9: Componente1.GND#66, LCD1.VSS
  N10: Componente1.GND#76, LCD1.V0
  N11: Componente1.5V#81, R5.Pin_0
  N12: Componente1.5V#95, LCD1.VDD

custom parts:
  Arduino Nano Expansion Board (Rev3.0): Arduino Nano 3.0 IO expansion board
