# Fritzing sketch lcd_i2c_leonardo (saved by Fritzing 0.9.3b)

parts:
  Display1 = LCD screen 16x2 I2C [part_number=101290]
  Componente2 = Arduino Leonardo (Rev3b)

nets:
  GND: Display1.GND, Componente2.GND
  VCC: Display1.VCC, Componente2.5V
  N1: Display1.SDA, Componente2.SDA
  N2: Display1.SCL, Componente2.SCL
