# Fritzing sketch lcd_i2c_nano (saved by Fritzing 0.9.3b)

parts:
  Componente1 = Arduino Nano Expansion Board (Rev3.0)
  Display1 = LCD screen 16x2 I2C [part_number=101290]

nets:
  GND: Componente1.GND, Display1.GND
  5V: Componente1.5V, Display1.VCC
  N1: Componente1.SCL, Display1.SCL
  N2: Componente1.SDA, Display1.SDA

custom parts:
  Arduino Nano Expansion Board (Rev3.0): Arduino Nano 3.0 IO expansion board
