# Fritzing sketch lcd_i2c_nodemcu (saved by Fritzing 0.9.3b)

parts:
  Display1 = LCD screen 16x2 I2C [part_number=101290]
  Componente1 = ESP12E Motor Shield

nets:
  GND: Display1.GND, Componente1.G, Componente1.GND
  VCC: Display1.VCC, Componente1.5V
  N1: Display1.SDA, Componente1.D2
  N2: Display1.SCL, Componente1.D1

custom parts:
  ESP12E Motor Shield: ESP8266 WiFi Motor Drive Expansion Board For NodeMCU ESP-12E
