# Fritzing sketch lcd_i2c_wemosD1R32 (saved by Fritzing 0.9.3b)

parts:
  Display1 = LCD screen 16x2 I2C [part_number=101290]
  WeMos_D1_R1 = WeMos D1 R32

nets:
  GND: Display1.GND, WeMos_D1_R1.GND
  VCC: Display1.VCC, WeMos_D1_R1.5V
  N1: Display1.SDA, WeMos_D1_R1.SDA
  N2: Display1.SCL, WeMos_D1_R1.SCL

custom parts:
  WeMos D1 R32: The D1 R32 is a mini wifi board based on the ESP32.
