# Fritzing sketch RGB_led_leonardo (saved by Fritzing 0.9.3b)

parts:
  Componente1 = Arduino Leonardo (Rev3b)
  Part1 = KY-016 RGB Full Color LED Module [package="Breakout board"]

nets:
  N1: Componente1.D2/SDA, Part1.R
  N2: Componente1.D3_PWM/SCL, Part1.G
  N3: Componente1.D4/A6, Part1.B
  N4: Componente1.GND, Part1.-

custom parts:
  KY-016 RGB Full Color LED Module: KY-016 Arduino full color 5mm RGB LED, different colors can be obtained by mixing the three primary colors.
