# Fritzing sketch RGB_led_nano (saved by Fritzing 0.9.3b)

parts:
  Part1 = KY-016 RGB Full Color LED Module [package="Breakout board"]
  Componente1 = Arduino Nano (Rev3.0)

nets:
  N1: Part1.-, Componente1.GND
  N2: Part1.R, Componente1.D2
  N3: Part1.G, Componente1.D3/PWM0
  N4: Part1.B, Componente1.D4, Componente1.5V

custom parts:
  KY-016 RGB Full Color LED Module: KY-016 Arduino full color 5mm RGB LED, different colors can be obtained by mixing the three primary colors.
  Arduino Nano (Rev3.0): Arduino Nano 3.0 IO expansion board
