# Fritzing sketch RGB_led_wemosD1R32 (saved by Fritzing 0.9.3b)

parts:
  Part1 = KY-016 RGB Full Color LED Module [package="Breakout board"]
  WeMos_D1_R32_Shield1 = WeMos D1 R32 with Arduino Sensor Shield v5

nets:
  N1: Part1.-, WeMos_D1_R32_Shield1.GND
  N2: Part1.R, WeMos_D1_R32_Shield1.D2
  N3: Part1.G, WeMos_D1_R32_Shield1.D3
  N4: Part1.B, WeMos_D1_R32_Shield1.D4

custom parts:
  KY-016 RGB Full Color LED Module: KY-016 Arduino full color 5mm RGB LED, different colors can be obtained by mixing the three primary colors.
  WeMos D1 R32 with Arduino Sensor Shield v5: The D1 R32 is a mini wifi board based on the ESP32 with an Arduino Sensor Shield v5
