# Fritzing sketch ledRGB_esp8266_example (saved by Fritzing 0.9.3b)

parts:
  Componente1 = NodeMcu base board
  Part1 = KY-016 RGB Full Color LED Module [package="Breakout board"]

nets:
  N1: Componente1.D0, Part1.B
  N2: Componente1.D1, Part1.G
  N3: Componente1.D2, Part1.R
  N4: Componente1.G, Componente1.GND, Part1.-

custom parts:
  NodeMcu base board: This is the based board shield for NodeMCU (Lolin)
  KY-016 RGB Full Color LED Module: KY-016 Arduino full color 5mm RGB LED, different colors can be obtained by mixing the three primary colors.
