# Fritzing sketch ledRGB_example (saved by Fritzing 0.9.3b)
breadboards: 1

parts:
  Parte1 = Arduino Nano (Rev3.0)
  LED1 = RGB LED - (4 legs) [package="5 mm [THT]"]
  R1 = Resistor [tolerance=±5% resistance=220 package="0402 [SMD]"]
  R2 = Resistor [tolerance=±5% resistance=220 package="0402 [SMD]"]
  R3 = Resistor [tolerance=±5% resistance=220 package="0402 [SMD]"]

nets:
  N1: Parte1.D2, R2.Pin_0
  N2: Parte1.D3/PWM0, R3.Pin_0
  N3: Parte1.D4, R1.Pin_0
  N4: Parte1.GND, LED1.common_anode
  N5: LED1.red_cathode, R2.Pin_1
  N6: LED1.green_cathode, R3.Pin_1
  N7: LED1.blue_cathode, R1.Pin_1

custom parts:
  Arduino Nano (Rev3.0): Arduino Nano 3.0 IO expansion board
