# Fritzing sketch ledRG_esp8266_example (saved by Fritzing 0.9.3b)
breadboards: 1

parts:
  Componente1 = NodeMcu base board
  Part1 = KY-011 Two Color LED Module [package="Breakout board"]

nets:
  N1: Componente1.D1, Part1.S
  N2: Componente1.D2, Part1.Vin
  N3: Componente1.GND, Part1.-

custom parts:
  NodeMcu base board: This is the based board shield for NodeMCU (Lolin)
  KY-011 Two Color LED Module: KEYES KY-011 Two Color LED Module consist of a common cathode 3mm red/green LED.
