# Fritzing sketch semaphore_leds_nano (saved by Fritzing 0.9.3b)

parts:
  Componente2 = Arduino Nano (Rev3.0)
  Part2 = Semaphore module

nets:
  N1: Componente2.D5/PWM1, Part2.G
  N2: Componente2.D6/PWM2, Part2.Y
  N3: Componente2.D7, Part2.R
  GND: Componente2.D11/PWM5, Componente2.GND, Part2.GND

custom parts:
  Arduino Nano (Rev3.0): Arduino Nano 3.0 IO expansion board
