# Fritzing sketch semaphore_leds_wemosD1R32 (saved by Fritzing 0.9.3b)

parts:
  Part2 = Semaphore module
  WeMos_D1_R32_Shield1 = WeMos D1 R32 with Arduino Sensor Shield v5

nets:
  GND: Part2.GND, WeMos_D1_R32_Shield1.GND
  N1: Part2.G, WeMos_D1_R32_Shield1.D5
  N2: Part2.R, WeMos_D1_R32_Shield1.D7
  N3: Part2.Y, WeMos_D1_R32_Shield1.D6

custom parts:
  WeMos D1 R32 with Arduino Sensor Shield v5: The D1 R32 is a mini wifi board based on the ESP32 with an Arduino Sensor Shield v5
