# Fritzing sketch two_leds_leonardo (saved by Fritzing 0.9.3b)
breadboards: 1

parts:
  LED1 = LED - 5mm [color="Red (633nm)" package="5 mm [THT]"]
  LED2 = LED - 5mm [color="Green (555nm)" package="5 mm [THT]"]
  R1 = Resistor [tolerance=±5% resistance=220 package="2512 [SMD]"]
  R2 = Resistor [tolerance=±5% resistance=220 package="2512 [SMD]"]
  Componente1 = Arduino Leonardo (Rev3b)

nets:
  N1: LED1.cathode, LED2.cathode, Componente1.GND
  N2: LED1.anode, R1.Pin_1
  N3: LED2.anode, R2.Pin_1
  N4: R1.Pin_0, Componente1.D2/SDA
  N5: R2.Pin_0, Componente1.D3_PWM/SCL
