# Fritzing sketch mic_example (saved by Fritzing 0.9.3b)

parts:
  Parte1 = Arduino Nano (Rev3.0)
  Componente1 = Breakout Board for Electret Microphone

nets:
  N1: Parte1.A1, Componente1.AUD
  GND: Parte1.GND, Componente1.GND
  5V: Parte1.5V, Componente1.VCC

custom parts:
  Arduino Nano (Rev3.0): Arduino Nano 3.0 IO expansion board
