# Fritzing sketch motors_dc_enc_example (saved by Fritzing 0.9.3b)

parts:
  Parte1 = Arduino Nano (Rev3.0)
  M1 = DC Motor
  M2 = DC Motor
  E1 = HC-020k
  E2 = HC-020k
  Componente2 = Adafruit DRV8833 DC/Stepper Motor Driver [part_number="Adafruit #3297"]

nets:
  N1: Parte1.D2, E2.Out
  N2: Parte1.D3/PWM0, E1.Out
  N3: Parte1.D5/PWM1, Componente2.IN1
  N4: Parte1.D6/PWM2, Componente2.IN2
  N5: Parte1.D9/PWM3, Componente2.IN3
  N6: Parte1.D10/PWM4, Componente2.IN4
  N7: Parte1.GND#56, Componente2.GND
  N8: Parte1.GND#62, E1.Gnd
  N9: Parte1.GND#63, E2.Gnd
  N10: Parte1.5V#85, Componente2.VCC
  N11: Parte1.5V#91, E1.Vcc
  N12: Parte1.5V#92, E2.Vcc
  N13: M1.pin_1, Componente2.OUT3
  N14: M1.pin_2, Componente2.OUT4
  N15: M2.pin_1, Componente2.OUT1
  N16: M2.pin_2, Componente2.OUT2

custom parts:
  Arduino Nano (Rev3.0): Arduino Nano 3.0 IO expansion board
  HC-020k: HC-020k Encoder module
  Adafruit DRV8833 DC/Stepper Motor Driver: Spin two DC motors or step one bi-polar or uni-polar stepper with up to 1.2A per channel using the DRV8833. This motor driver chip is a nice alternative to the TB6612 driver. Like that chip, you get 2 full H-bridges, but this chip is better for low voltage uses (can run from 2.7V up to 10.8V motor power) and has built in current limiting capability. We set it up for 1A current limiting so you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
