# Fritzing sketch motors_dc_example (saved by Fritzing 0.9.3b)

parts:
  Parte1 = Arduino Nano (Rev3.0)
  Componente1 = Adafruit DRV8833 DC/Stepper Motor Driver [part_number="Adafruit #3297"]
  M1 = DC Motor
  VCC1 = Battery block 9V
  M2 = DC Motor

nets:
  N1: Parte1.D3/PWM0, Componente1.AIN1
  N2: Parte1.D5/PWM1, Componente1.AIN2
  N3: Parte1.D6/PWM2, Componente1.BIN1
  N4: Parte1.D9/PWM3, Componente1.BIN2
  N5: Parte1.GND#60, VCC1.-
  N6: Parte1.GND#62, Componente1.GND
  N7: Componente1.AOUT2, M1.pin_1
  N8: Componente1.AOUT1, M1.pin_2
  N9: Componente1.BOUT1, M2.pin_1
  N10: Componente1.BOUT2, M2.pin_2
  N11: Componente1.VMOTOR, VCC1.+

custom parts:
  Arduino Nano (Rev3.0): Arduino Nano 3.0 IO expansion board
  Adafruit DRV8833 DC/Stepper Motor Driver: Spin two DC motors or step one bi-polar or uni-polar stepper with up to 1.2A per channel using the DRV8833. This motor driver chip is a nice alternative to the TB6612 driver. Like that chip, you get 2 full H-bridges, but this chip is better for low voltage uses (can run from 2.7V up to 10.8V motor power) and has built in current limiting capability. We set it up for 1A current limiting so you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
