# Fritzing sketch multisensor_uno_LCD (saved by Fritzing 0.9.3b)

parts:
  Componente3 = Arduino Uno with Shield
  Display3 = LCD screen 16x2 I2C [part_number=101290]

nets:
  N1: Componente3.A4/SDA, Display3.SDA
  N2: Componente3.A5/SCL, Display3.SCL
  GND: Componente3.GND, Display3.GND
  5V: Componente3.5V, Display3.VCC

custom parts:
  Arduino Uno with Shield: Arduino Uno with sensor shield v5
