# Fritzing sketch multisensor_uno_LCD_modules (saved by Fritzing 0.9.3b)

parts:
  Componente4 = Arduino Uno with Shield
  Display3 = LCD screen 16x2 I2C [part_number=101290]

nets:
  N1: Componente4.A4/SDA, Display3.SDA
  N2: Componente4.A5/SCL, Display3.SCL
  GND: Componente4.GND, Display3.GND
  5V: Componente4.5V, Display3.VCC

custom parts:
  Arduino Uno with Shield: Arduino Uno with sensor shield v5
