# Fritzing sketch multisensor_uno_LCD_pushbutton (saved by Fritzing 0.9.3b)
breadboards: 1

parts:
  Display2 = LCD screen 16x2 I2C [part_number=101290]
  R16 = Resistor [tolerance=±5% resistance=3.3k package="1206 [SMD]"]
  SW5 = Pushbutton [package=THT]
  Componente1 = Arduino Uno (Rev3)

nets:
  GND: Display2.GND, SW5.leg0, Componente1.GND
  VCC: Display2.VCC, R16.Pin_0, Componente1.5V
  N1: Display2.SDA, Componente1.A4/SDA
  N2: Display2.SCL, Componente1.A5/SCL
  N3: R16.Pin_1, SW5.leg1
