# Fritzing sketch multisensor_uno_LCD_pushbutton_modules (saved by Fritzing 0.9.3b)

parts:
  Componente4 = Arduino Uno with Shield
  Display3 = LCD screen 16x2 I2C [part_number=101290]
  Part2 = KY-004 Key Switch Module [package="Breakout board"]

nets:
  N1: Componente4.A4/SDA, Display3.SDA
  N2: Componente4.A5/SCL, Display3.SCL
  N3: Componente4.D2, Part2.S
  N4: Componente4.GND#86, Part2.-
  N5: Componente4.5V#108, Part2.Vin
  N6: Componente4.GND#128, Display3.GND
  N7: Componente4.5V#129, Display3.VCC

custom parts:
  Arduino Uno with Shield: Arduino Uno with sensor shield v5
  KY-004 Key Switch Module: Arduino Key Switch Module Keyes KY-004 is a push button that will output a high signal when pressed.
