# Fritzing sketch multisensor_uno_LEDs_pushbuttons (saved by Fritzing 0.9.3b)
breadboards: 1

parts:
  R9 = Resistor [tolerance=±5% resistance=3.3k package="1206 [SMD]"]
  R10 = Resistor [tolerance=±5% resistance=3.3k package="1206 [SMD]"]
  LED1_D14 = smd LED [color="Blue (430nm)" package="0805 [SMD]"]
  LED2_D13 = smd LED [color="Red (633nm)" package="0805 [SMD]"]
  SW2 = Pushbutton [package=THT]
  R11 = Resistor [tolerance=±5% resistance=3.3k package="1206 [SMD]"]
  Componente1 = Arduino Uno (Rev3)
  S2 = Pushbutton [package=THT]
  R13 = Resistor [tolerance=±5% resistance=220 package="1206 [SMD]"]

nets:
  N1: R9.Pin_0, Componente1.D12/MISO
  N2: R9.Pin_1, LED2_D13.anode
  N3: R10.Pin_0, Componente1.D13/SCK
  N4: R10.Pin_1, LED1_D14.anode
  N5: LED1_D14.cathode, LED2_D13.cathode, SW2.leg0, Componente1.GND, S2.leg0
  N6: SW2.leg1, R11.Pin_1, Componente1.D2
  N7: R11.Pin_0, Componente1.5V, R13.Pin_0
  N8: Componente1.D3_PWM, S2.leg1, R13.Pin_1
