# Fritzing sketch multisensor_uno_RGB (saved by Fritzing 0.9.3b)
breadboards: 1

parts:
  R4 = Resistor [tolerance=±5% resistance=3.3k package="1206 [SMD]"]
  R5 = Resistor [tolerance=±5% resistance=3.3k package="1206 [SMD]"]
  R6 = Resistor [tolerance=±5% resistance=3.3k package="1206 [SMD]"]
  RGB_LED_D9-D11 = RGB LED (com. cathode, rgb) [package="5 mm [THT]"]
  Componente1 = Arduino Uno (Rev3)

nets:
  N1: R4.Pin_1, RGB_LED_D9-D11.red_anode
  N2: R5.Pin_0, Componente1.D11_PWM/MOSI
  N3: R5.Pin_1, RGB_LED_D9-D11.green_anode
  N4: R6.Pin_1, RGB_LED_D9-D11.blue_anode
  N5: RGB_LED_D9-D11.common_cathode, Componente1.GND
