# Fritzing sketch multisensor_uno_RGB_IR_buzzer (saved by Fritzing 0.9.3b)
breadboards: 1

parts:
  R4 = Resistor [tolerance=±5% resistance=3.3k package="1206 [SMD]"]
  R5 = Resistor [tolerance=±5% resistance=3.3k package="1206 [SMD]"]
  R6 = Resistor [tolerance=±5% resistance=3.3k package="1206 [SMD]"]
  RGB_LED_D9-D11 = RGB LED (com. cathode, rgb) [package="5 mm [THT]"]
  Componente1 = Arduino Uno (Rev3)
  IR1 = TSOP312.., 314.. [package=THT]
  Q4 = NPN-Transistor [package="SOT-23 [SMD]"]
  Buzzer_D8 = Piezo Speaker
  R13 = Resistor [tolerance=±5% resistance=3.3k package="1206 [SMD]"]

nets:
  N1: R4.Pin_1, RGB_LED_D9-D11.red_anode
  N2: R5.Pin_0, Componente1.D11_PWM/MOSI
  N3: R5.Pin_1, RGB_LED_D9-D11.green_anode
  N4: R6.Pin_1, RGB_LED_D9-D11.blue_anode
  GND: RGB_LED_D9-D11.common_cathode, Componente1.GND, IR1.GND, Buzzer_D8.pin1
  N5: Componente1.D5_PWM, Q4.0
  N6: Componente1.D6_PWM, IR1.Data
  N7: Componente1.5V, IR1.Vs, R13.Pin_0
  N8: Q4.2, Buzzer_D8.pin2
  N9: Q4.1, R13.Pin_1

custom parts:
  Piezo Speaker: Piezo
