# Fritzing sketch multisensor_uno_RGB_IR_buzzer_modules (saved by Fritzing 0.9.3b)

parts:
  Part2 = KY-016 RGB Full Color LED Module [package="Breakout board"]
  Componente4 = Arduino Uno with Shield
  Part4 = KY-022 Infrared Receiver Module [package="Breakout board"]
  Part5 = KY-006 Passive Buzzer Module [package="Breakout board"]

nets:
  N1: Part2.-, Componente4.GND#95
  N2: Part2.R, Componente4.D9_PWM
  N3: Part2.G, Componente4.D11_PWM/MOSI
  N4: Part2.B, Componente4.D10_PWM/SS
  N5: Componente4.D5_PWM, Part5.S
  N6: Componente4.D6_PWM, Part4.S
  N7: Componente4.GND#89, Part5.-
  N8: Componente4.GND#90, Part4.-
  N9: Componente4.5V#111, Part5.+5V
  N10: Componente4.5V#112, Part4.Vin

custom parts:
  KY-016 RGB Full Color LED Module: KY-016 Arduino full color 5mm RGB LED, different colors can be obtained by mixing the three primary colors.
  Arduino Uno with Shield: Arduino Uno with sensor shield v5
  KY-022 Infrared Receiver Module: Arduino IR receiver module KY-022, reacts to 38kHz infrared light.
  KY-006 Passive Buzzer Module: Passive Piezoelectric Buzzer Module Keyes KY-006, it can produce a range of sound tones depending on the input frequency.
