# Fritzing sketch multisensor_uno_RGB_ldr_modules (saved by Fritzing 0.9.3b)

parts:
  Part2 = KY-016 RGB Full Color LED Module [package="Breakout board"]
  Componente4 = Arduino Uno with Shield
  R2 = Photocell (LDR) [package=THT]

nets:
  N1: Part2.-, Componente4.GND#95
  N2: Part2.R, Componente4.D9_PWM
  N3: Part2.G, Componente4.D11_PWM/MOSI
  N4: Part2.B, Componente4.D10_PWM/SS
  N5: Componente4.A0, R2.S
  N6: Componente4.GND#100, R2.-
  N7: Componente4.5V, R2.+

custom parts:
  KY-016 RGB Full Color LED Module: KY-016 Arduino full color 5mm RGB LED, different colors can be obtained by mixing the three primary colors.
  Arduino Uno with Shield: Arduino Uno with sensor shield v5
  Photocell (LDR): A generic light dependent resistor (LDR)
