# Fritzing sketch multisensor_uno_RGB_pushbutton_buzzer (saved by Fritzing 0.9.3b)
breadboards: 1

parts:
  SW2 = Pushbutton [package=THT]
  R11 = Resistor [tolerance=±5% resistance=3.3k package="1206 [SMD]"]
  Q3 = NPN-Transistor [package="SOT-23 [SMD]"]
  Buzzer_D7 = Piezo Speaker
  R12 = Resistor [tolerance=±5% resistance=3.3k package="1206 [SMD]"]
  Componente1 = Arduino Uno (Rev3)
  R16 = Resistor [tolerance=±5% resistance=3.3k package="1206 [SMD]"]
  R17 = Resistor [tolerance=±5% resistance=3.3k package="1206 [SMD]"]
  R18 = Resistor [tolerance=±5% resistance=3.3k package="1206 [SMD]"]
  LED3 = RGB LED (com. cathode, rgb) [package="5 mm [THT]"]

nets:
  N1: SW2.leg0, Buzzer_D7.pin1, Componente1.GND, LED3.common_cathode
  N2: SW2.leg1, R11.Pin_1, Componente1.D2
  N3: R11.Pin_0, Q3.1, R12.Pin_1, Componente1.5V
  N4: Q3.2, Buzzer_D7.pin2
  N5: Q3.0, Componente1.D5_PWM
  N6: Componente1.D9_PWM, R16.Pin_1
  N7: Componente1.D10_PWM/SS, R17.Pin_0
  N8: Componente1.D11_PWM/MOSI, R18.Pin_0
  N9: R16.Pin_0, LED3.red_anode
  N10: R17.Pin_1, LED3.blue_anode
  N11: R18.Pin_1, LED3.green_anode

custom parts:
  Piezo Speaker: Piezo
