# Fritzing sketch multisensor_uno_bluetooth (saved by Fritzing 0.9.3b)

parts:
  Componente3 = Arduino Uno with Shield
  Componente4 = Bluetooth HC-05 Macho

nets:
  N1: Componente3.D8, Componente4.TXD
  N2: Componente3.D7, Componente4.RXD
  GND: Componente3.GND, Componente4.GND
  5V: Componente3.5V, Componente4.VCC

custom parts:
  Arduino Uno with Shield: Arduino Uno with sensor shield v5
