# Fritzing sketch multisensor_uno_dht11 (saved by Fritzing 0.9.3b)
breadboards: 1

parts:
  DHT11_D4 = DHT11 Humitidy and Temperature Sensor
  Componente1 = Arduino Uno (Rev3)

nets:
  VDD: DHT11_D4.VDD, Componente1.5V
  N1: DHT11_D4.DATA, Componente1.D4
  GND: DHT11_D4.GND, Componente1.GND

custom parts:
  DHT11 Humitidy and Temperature Sensor: DHT11 Humidity and Temperature Sensor
