# Fritzing sketch multisensor_uno_dht11_modules (saved by Fritzing 0.9.3b)

parts:
  DHT1 = DHT11 Humitidy and Temperature Sensor
  Componente2 = Arduino Uno with Shield

nets:
  VDD: DHT1.VDD, Componente2.5V
  N1: DHT1.S, Componente2.D4
  GND: DHT1.GND, Componente2.GND

custom parts:
  DHT11 Humitidy and Temperature Sensor: DHT11 Humidity and Temperature Sensor
  Arduino Uno with Shield: Arduino Uno with sensor shield v5
