# Fritzing sketch multisensor_uno_gas_LED_pushbutton_buzzer (saved by Fritzing 0.9.3b)
breadboards: 1

parts:
  SW2 = Pushbutton [package=THT]
  R11 = Resistor [tolerance=±5% resistance=3.3k package="1206 [SMD]"]
  Q3 = NPN-Transistor [package="SOT-23 [SMD]"]
  Buzzer_D7 = Piezo Speaker
  R12 = Resistor [tolerance=±5% resistance=3.3k package="1206 [SMD]"]
  Componente1 = Arduino Uno (Rev3)
  R16 = Resistor [tolerance=±5% resistance=3.3k package="1206 [SMD]"]
  LED2_D15 = smd LED [color="Red (633nm)" package="0805 [SMD]"]
  Componente7 = MQ-3 breakout

nets:
  GND: SW2.leg0, Buzzer_D7.pin1, Componente1.GND, R16.Pin_0, Componente7.GND
  N1: SW2.leg1, R11.Pin_1, Componente1.D2
  5V: R11.Pin_0, Q3.1, R12.Pin_1, Componente1.5V, Componente7.VCC
  N2: Q3.2, Buzzer_D7.pin2
  N3: Q3.0, Componente1.D5_PWM
  N4: Componente1.A3, Componente7.AO
  N5: Componente1.D8, Componente7.DO
  N6: Componente1.D9_PWM, LED2_D15.anode
  N7: R16.Pin_1, LED2_D15.cathode

custom parts:
  Piezo Speaker: Piezo
  MQ-3 breakout: Alcohol sensor is capable of detecting alcohol (ethanol) particles on itself and gives the information in digital form back to us to manipulate with it. SKU:101251 • Voltage: 5V DC • Power: max 750mW • Measurement range: 0.04-4mg/L
