# Fritzing sketch multisensor_uno_gas_LED_pushbutton_buzzer_modules (saved by Fritzing 0.9.3b)

parts:
  Part1 = KY-004 Key Switch Module [package="Breakout board"]
  Componente4 = Arduino Uno with Shield
  Part6 = KY-006 Passive Buzzer Module [package="Breakout board"]
  Part7 = KY-016 RGB Full Color LED Module [package="Breakout board"]
  Componente6 = MQ-3 breakout

nets:
  N1: Part1.S, Componente4.D2
  N2: Part1.Vin, Componente4.5V#108
  N3: Part1.-, Componente4.GND#86
  N4: Componente4.A3, Componente6.AO
  N5: Componente4.D8, Componente6.DO
  N6: Componente4.D12/MISO, Part7.R
  N7: Componente4.D5_PWM, Part6.S
  N8: Componente4.GND#89, Part6.-
  N9: Componente4.GND#96, Part7.-
  N10: Componente4.GND#103, Componente6.GND
  N11: Componente4.5V#111, Part6.+5V
  N12: Componente4.5V#125, Componente6.VCC

custom parts:
  KY-004 Key Switch Module: Arduino Key Switch Module Keyes KY-004 is a push button that will output a high signal when pressed.
  Arduino Uno with Shield: Arduino Uno with sensor shield v5
  KY-006 Passive Buzzer Module: Passive Piezoelectric Buzzer Module Keyes KY-006, it can produce a range of sound tones depending on the input frequency.
  KY-016 RGB Full Color LED Module: KY-016 Arduino full color 5mm RGB LED, different colors can be obtained by mixing the three primary colors.
  MQ-3 breakout: Alcohol sensor is capable of detecting alcohol (ethanol) particles on itself and gives the information in digital form back to us to manipulate with it. SKU:101251 • Voltage: 5V DC • Power: max 750mW • Measurement range: 0.04-4mg/L
