# Fritzing sketch multisensor_uno_multisensor_gas (saved by Fritzing 0.9.3b)

parts:
  Componente3 = Arduino Uno with Shield
  Componente4 = MQ-3 breakout

nets:
  N1: Componente3.A3, Componente4.AO
  N2: Componente3.D8, Componente4.DO
  GND: Componente3.GND, Componente4.GND
  5V: Componente3.5V, Componente4.VCC

custom parts:
  Arduino Uno with Shield: Arduino Uno with sensor shield v5
  MQ-3 breakout: Alcohol sensor is capable of detecting alcohol (ethanol) particles on itself and gives the information in digital form back to us to manipulate with it. SKU:101251 • Voltage: 5V DC • Power: max 750mW • Measurement range: 0.04-4mg/L
