# Fritzing sketch multisensor_uno_pot (saved by Fritzing 0.9.3b)
breadboards: 1

parts:
  Rotation_A0 = POT [package=alps_pot]
  Componente1 = Arduino Uno (Rev3)

nets:
  N1: Rotation_A0.E, Componente1.5V
  N2: Rotation_A0.S, Componente1.A0
  N3: Rotation_A0.A, Componente1.GND
