# Fritzing sketch multisensor_uno_pot_LED_pushbutton (saved by Fritzing 0.9.3b)
breadboards: 1

parts:
  R9 = Resistor [tolerance=±5% resistance=3.3k package="1206 [SMD]"]
  LED2_D13 = smd LED [color="Red (633nm)" package="0805 [SMD]"]
  SW2 = Pushbutton [package=THT]
  R11 = Resistor [tolerance=±5% resistance=3.3k package="1206 [SMD]"]
  Componente1 = Arduino Uno (Rev3)
  Rotation_A1 = POT [package=alps_pot]

nets:
  N1: R9.Pin_0, Componente1.D12/MISO
  N2: R9.Pin_1, LED2_D13.anode
  N3: LED2_D13.cathode, SW2.leg0, Componente1.GND, Rotation_A1.A
  N4: SW2.leg1, R11.Pin_1, Componente1.D2
  N5: R11.Pin_0, Componente1.5V, Rotation_A1.E
  N6: Componente1.A0, Rotation_A1.S
