# Fritzing sketch multisensor_uno_pot_LEDs_buzzer (saved by Fritzing 0.9.3b)
breadboards: 1

parts:
  R9 = Resistor [tolerance=±5% resistance=3.3k package="1206 [SMD]"]
  R10 = Resistor [tolerance=±5% resistance=3.3k package="1206 [SMD]"]
  LED1_D14 = smd LED [color="Blue (430nm)" package="0805 [SMD]"]
  LED2_D13 = smd LED [color="Red (633nm)" package="0805 [SMD]"]
  R11 = Resistor [tolerance=±5% resistance=3.3k package="1206 [SMD]"]
  Componente1 = Arduino Uno (Rev3)
  SW3 = Pushbutton [package=THT]
  Q2 = NPN-Transistor [package="SOT-23 [SMD]"]
  R12 = Resistor [tolerance=±5% resistance=3.3k package="1206 [SMD]"]
  Buzzer_D8 = Piezo Speaker

nets:
  N1: R9.Pin_0, Componente1.D12/MISO
  N2: R9.Pin_1, LED2_D13.anode
  N3: R10.Pin_0, Componente1.D13/SCK
  N4: R10.Pin_1, LED1_D14.anode
  N5: LED1_D14.cathode, LED2_D13.cathode, Componente1.GND, SW3.leg0, R12.Pin_0, Buzzer_D8.pin1
  N6: R11.Pin_0, Componente1.5V
  N7: R11.Pin_1, Componente1.D2, SW3.leg1
  N8: Componente1.D5_PWM, Q2.0
  N9: Q2.2, Buzzer_D8.pin2
  N10: Q2.1, R12.Pin_1

custom parts:
  Piezo Speaker: Piezo
