# Fritzing sketch multisensor_uno_pot_LEDs_buzzer_modules (saved by Fritzing 0.9.3b)

parts:
  Part2 = KY-016 RGB Full Color LED Module [package="Breakout board"]
  Componente4 = Arduino Uno with Shield
  Part4 = Potentiometer module [package="Breakout board"]
  Part5 = KY-006 Passive Buzzer Module [package="Breakout board"]

nets:
  N1: Part2.-, Componente4.GND#97
  N2: Part2.R, Componente4.D12/MISO
  N3: Part2.B, Componente4.D13/SCK
  N4: Componente4.A0, Part4.S
  N5: Componente4.D5_PWM, Part5.S
  N6: Componente4.GND#89, Part5.-
  N7: Componente4.GND#100, Part4.-
  N8: Componente4.5V#111, Part5.+5V
  N9: Componente4.5V#122, Part4.Vin

custom parts:
  KY-016 RGB Full Color LED Module: KY-016 Arduino full color 5mm RGB LED, different colors can be obtained by mixing the three primary colors.
  Arduino Uno with Shield: Arduino Uno with sensor shield v5
  Potentiometer module: A potentiometer module
  KY-006 Passive Buzzer Module: Passive Piezoelectric Buzzer Module Keyes KY-006, it can produce a range of sound tones depending on the input frequency.
