# Fritzing sketch multisensor_uno_pot_LEDs_ldr_lm35 (saved by Fritzing 0.9.3b)
breadboards: 1

parts:
  R9 = Resistor [tolerance=±5% resistance=3.3k package="1206 [SMD]"]
  R10 = Resistor [tolerance=±5% resistance=3.3k package="1206 [SMD]"]
  LED1_D14 = smd LED [color="Blue (430nm)" package="0805 [SMD]"]
  LED2_D13 = smd LED [color="Red (633nm)" package="0805 [SMD]"]
  R11 = Resistor [tolerance=±5% resistance=3.3k package="1206 [SMD]"]
  Componente1 = Arduino Uno (Rev3)
  Rotation_A1 = POT [package=alps_pot]
  LDR_A3 = Photocell (LDR) [package=THT]
  LM35_A4 = LM35 Temperature Sensor [package="TO92 [THT]"]

nets:
  N1: R9.Pin_0, Componente1.D12/MISO
  N2: R9.Pin_1, LED2_D13.anode
  N3: R10.Pin_0, Componente1.D13/SCK
  N4: R10.Pin_1, LED1_D14.anode
  GND: LED1_D14.cathode, LED2_D13.cathode, Componente1.GND, Rotation_A1.A, LDR_A3.pin_0, LM35_A4.GND
  N5: R11.Pin_0, Componente1.A1, LDR_A3.pin_1
  N6: R11.Pin_1, Componente1.5V, Rotation_A1.E, LM35_A4.+Vs
  N7: Componente1.A0, Rotation_A1.S
  N8: Componente1.A2, LM35_A4.Vout
