# Fritzing sketch multisensor_uno_pot_LEDs_ldr_lm35_modules (saved by Fritzing 0.9.3b)

parts:
  Part2 = KY-016 RGB Full Color LED Module [package="Breakout board"]
  Componente4 = Arduino Uno with Shield
  Part4 = Potentiometer module [package="Breakout board"]
  R1 = Photocell (LDR) [package=THT]
  Part6 = LM35 [package="Breakout board"]

nets:
  N1: Part2.-, Componente4.GND#97
  N2: Part2.R, Componente4.D12/MISO
  N3: Part2.B, Componente4.D13/SCK
  N4: Componente4.A0, Part4.S
  N5: Componente4.A1, R1.S
  N6: Componente4.A2, Part6.S
  N7: Componente4.GND#100, Part4.-
  N8: Componente4.GND#101, R1.-
  N9: Componente4.GND#102, Part6.-
  N10: Componente4.5V#122, Part4.Vin
  N11: Componente4.5V#123, R1.+
  N12: Componente4.5V#124, Part6.Vin

custom parts:
  KY-016 RGB Full Color LED Module: KY-016 Arduino full color 5mm RGB LED, different colors can be obtained by mixing the three primary colors.
  Arduino Uno with Shield: Arduino Uno with sensor shield v5
  Potentiometer module: A potentiometer module
  Photocell (LDR): A generic light dependent resistor (LDR)
  LM35: Arduino Temperature Sensor Module LM35
