# Fritzing sketch multisensor_uno_pot_LEDs_pushbutton_modules (saved by Fritzing 0.9.3b)

parts:
  Part1 = KY-004 Key Switch Module [package="Breakout board"]
  Part2 = KY-016 RGB Full Color LED Module [package="Breakout board"]
  Componente4 = Arduino Uno with Shield
  Part4 = Potentiometer module [package="Breakout board"]

nets:
  N1: Part1.S, Componente4.D2
  N2: Part1.Vin, Componente4.5V#108
  N3: Part1.-, Componente4.GND#86
  N4: Part2.-, Componente4.GND#97
  N5: Part2.R, Componente4.D12/MISO
  N6: Part2.B, Componente4.D13/SCK
  N7: Componente4.A0, Part4.S
  N8: Componente4.GND#100, Part4.-
  N9: Componente4.5V#122, Part4.Vin

custom parts:
  KY-004 Key Switch Module: Arduino Key Switch Module Keyes KY-004 is a push button that will output a high signal when pressed.
  KY-016 RGB Full Color LED Module: KY-016 Arduino full color 5mm RGB LED, different colors can be obtained by mixing the three primary colors.
  Arduino Uno with Shield: Arduino Uno with sensor shield v5
  Potentiometer module: A potentiometer module
