# Fritzing sketch multisensor_uno_pot_LEDs_pushbuttons_modules (saved by Fritzing 0.9.3b)

parts:
  Part1 = KY-004 Key Switch Module [package="Breakout board"]
  Componente4 = Arduino Uno with Shield
  Part5 = KY-004 Key Switch Module [package="Breakout board"]
  Part4 = Potentiometer module [package="Breakout board"]
  Part2 = KY-016 RGB Full Color LED Module [package="Breakout board"]

nets:
  N1: Part1.S, Componente4.D2
  N2: Part1.Vin, Componente4.5V#108
  N3: Part1.-, Componente4.GND#86
  N4: Componente4.A0, Part4.S
  N5: Componente4.D12/MISO, Part2.R
  N6: Componente4.D13/SCK, Part2.B
  N7: Componente4.D3_PWM, Part5.S
  N8: Componente4.GND#87, Part5.-
  N9: Componente4.GND#97, Part2.-
  N10: Componente4.GND#100, Part4.-
  N11: Componente4.5V#109, Part5.Vin
  N12: Componente4.5V#122, Part4.Vin

custom parts:
  KY-004 Key Switch Module: Arduino Key Switch Module Keyes KY-004 is a push button that will output a high signal when pressed.
  Arduino Uno with Shield: Arduino Uno with sensor shield v5
  Potentiometer module: A potentiometer module
  KY-016 RGB Full Color LED Module: KY-016 Arduino full color 5mm RGB LED, different colors can be obtained by mixing the three primary colors.
