# Fritzing sketch multisensor_uno_pot_modules (saved by Fritzing 0.9.3b)

parts:
  Part3 = Potentiometer module [package="Breakout board"]
  Componente1 = Arduino Uno with Shield

nets:
  N1: Part3.S, Componente1.A0
  VIN: Part3.Vin, Componente1.5V
  N2: Part3.-, Componente1.GND

custom parts:
  Potentiometer module: A potentiometer module
  Arduino Uno with Shield: Arduino Uno with sensor shield v5
