# Fritzing sketch multisensor_uno_pushbuttons_buzzer (saved by Fritzing 0.9.3b)
breadboards: 1

parts:
  R10 = Resistor [tolerance=±5% resistance=3.3k package="1206 [SMD]"]
  SW2 = Pushbutton [package=THT]
  R11 = Resistor [tolerance=±5% resistance=3.3k package="1206 [SMD]"]
  Q3 = NPN-Transistor [package="SOT-23 [SMD]"]
  Buzzer_D7 = Piezo Speaker
  R12 = Resistor [tolerance=±5% resistance=3.3k package="1206 [SMD]"]
  SW3 = Pushbutton [package=THT]
  Componente1 = Arduino Uno (Rev3)

nets:
  N1: R10.Pin_0, SW3.leg1, Componente1.D3_PWM
  N2: R10.Pin_1, R11.Pin_0, Q3.1, R12.Pin_1, Componente1.5V
  N3: SW2.leg0, Buzzer_D7.pin1, SW3.leg0, Componente1.GND
  N4: SW2.leg1, R11.Pin_1, Componente1.D2
  N5: Q3.2, Buzzer_D7.pin2
  N6: Q3.0, Componente1.D5_PWM

custom parts:
  Piezo Speaker: Piezo
