# Fritzing sketch multisensor_uno_pushbuttons_buzzer_modules (saved by Fritzing 0.9.3b)

parts:
  Part1 = KY-004 Key Switch Module [package="Breakout board"]
  Componente4 = Arduino Uno with Shield
  Part5 = KY-004 Key Switch Module [package="Breakout board"]
  Part6 = KY-006 Passive Buzzer Module [package="Breakout board"]

nets:
  N1: Part1.S, Componente4.D2
  N2: Part1.Vin, Componente4.5V#108
  N3: Part1.-, Componente4.GND#86
  N4: Componente4.D3_PWM, Part5.S
  N5: Componente4.D5_PWM, Part6.S
  N6: Componente4.GND#87, Part5.-
  N7: Componente4.GND#89, Part6.-
  N8: Componente4.5V#109, Part5.Vin
  N9: Componente4.5V#111, Part6.+5V

custom parts:
  KY-004 Key Switch Module: Arduino Key Switch Module Keyes KY-004 is a push button that will output a high signal when pressed.
  Arduino Uno with Shield: Arduino Uno with sensor shield v5
  KY-006 Passive Buzzer Module: Passive Piezoelectric Buzzer Module Keyes KY-006, it can produce a range of sound tones depending on the input frequency.
