# Fritzing sketch multisensor_uno_servo_relay_fan (saved by Fritzing 0.9.3b)

parts:
  Componente3 = Arduino Uno with Shield
  KY-4 = Keyes Relay [package=THT]
  COMPUTER_FAN4 = Computer fan
  J4 = Basic Servo

nets:
  N1: Componente3.D8, J4.pulse
  N2: Componente3.D7, KY-4.signal
  N3: Componente3.GND#101, COMPUTER_FAN4.BLACK
  N4: Componente3.GND#102, KY-4.ground
  N5: Componente3.GND#103, J4.gnd
  N6: Componente3.5V#124, KY-4.power
  N7: Componente3.5V#125, J4.vcc
  N8: Componente3.5V#126, KY-4.C
  N9: KY-4.NO, COMPUTER_FAN4.RED

custom parts:
  Arduino Uno with Shield: Arduino Uno with sensor shield v5
  Keyes Relay: The Keyes 5V relay module is suitable for SCM development, home appliance control. It uses a 5V~12V TIL control signal which can control DC / AC signal.
  Computer fan: This is a 5V computer fan
