# Fritzing sketch multisensor_uno_servo_relay_fan_pot_pushbutton (saved by Fritzing 0.9.3b)
breadboards: 1

parts:
  SW2 = Pushbutton [package=THT]
  R11 = Resistor [tolerance=±5% resistance=3.3k package="1206 [SMD]"]
  Componente1 = Arduino Uno (Rev3)
  Rotation_A1 = POT [package=alps_pot]
  KY-4 = Keyes Relay [package=THT]
  COMPUTER_FAN4 = Computer fan
  J4 = Basic Servo

nets:
  GND: SW2.leg0, Componente1.GND, Rotation_A1.A, KY-4.ground, COMPUTER_FAN4.BLACK, J4.gnd
  N1: SW2.leg1, R11.Pin_1, Componente1.D2
  5V: R11.Pin_0, Componente1.5V, Rotation_A1.E, KY-4.power, KY-4.C, J4.vcc
  N2: Componente1.A0, Rotation_A1.S
  N3: Componente1.D8, J4.pulse
  N4: Componente1.D7, KY-4.signal
  N5: KY-4.NO, COMPUTER_FAN4.RED

custom parts:
  Keyes Relay: The Keyes 5V relay module is suitable for SCM development, home appliance control. It uses a 5V~12V TIL control signal which can control DC / AC signal.
  Computer fan: This is a 5V computer fan
