# Fritzing sketch multisensor_uno_servo_relay_fan_pot_pushbutton_modules (saved by Fritzing 0.9.3b)

parts:
  Part1 = KY-004 Key Switch Module [package="Breakout board"]
  Componente4 = Arduino Uno with Shield
  Part4 = Potentiometer module [package="Breakout board"]
  KY-3 = Keyes Relay [package=THT]
  COMPUTER_FAN3 = Computer fan
  J3 = Basic Servo

nets:
  N1: Part1.S, Componente4.D2
  N2: Part1.Vin, Componente4.5V#108
  N3: Part1.-, Componente4.GND#86
  N4: Componente4.A0, Part4.S
  N5: Componente4.D8, J3.pulse
  N6: Componente4.D7, KY-3.signal
  N7: Componente4.GND#91, KY-3.ground
  N8: Componente4.GND#92, J3.gnd
  N9: Componente4.GND#99, COMPUTER_FAN3.BLACK
  N10: Componente4.GND#100, Part4.-
  N11: Componente4.5V#113, KY-3.power
  N12: Componente4.5V#114, J3.vcc
  N13: Componente4.5V#121, KY-3.C
  N14: Componente4.5V#122, Part4.Vin
  N15: KY-3.NO, COMPUTER_FAN3.RED

custom parts:
  KY-004 Key Switch Module: Arduino Key Switch Module Keyes KY-004 is a push button that will output a high signal when pressed.
  Arduino Uno with Shield: Arduino Uno with sensor shield v5
  Potentiometer module: A potentiometer module
  Keyes Relay: The Keyes 5V relay module is suitable for SCM development, home appliance control. It uses a 5V~12V TIL control signal which can control DC / AC signal.
  Computer fan: This is a 5V computer fan
