# Fritzing sketch multisensor_wemosD1R32_ACLightDimmer (saved by Fritzing 0.9.3b)

parts:
  WeMos_D1_R1 = WeMos D1 R32
  AC_Light_Dimmer1 = AC Light Dimmer
  AC_PLUG1 = AC Plug
  L1 = LED Light [package=THT]  # not connected
  L2 = LED Light Transformer [package=THT]

nets:
  N1: WeMos_D1_R1.IO14, AC_Light_Dimmer1.Z-C
  N2: WeMos_D1_R1.IO12, AC_Light_Dimmer1.PWM
  GND: WeMos_D1_R1.GND, AC_Light_Dimmer1.GND
  5V: WeMos_D1_R1.5V, AC_Light_Dimmer1.VCC
  N3: AC_PLUG1.RED, L2.L
  N4: AC_PLUG1.BLACK, L2.N

custom parts:
  WeMos D1 R32: The D1 R32 is a mini wifi board based on the ESP32.
  AC Light Dimmer: RoboDyn AC Light Dimmer
  AC Plug: This is a 220V/110 Vac plug
