# Fritzing sketch multisensor_wemosD1R32_Fan (saved by Fritzing 0.9.3b)

parts:
  WeMos_D1_R1 = WeMos D1 R32
  KY-1 = Keyes Relay [package=THT]
  COMPUTER_FAN1 = Computer fan

nets:
  N1: WeMos_D1_R1.GND#20, KY-1.ground
  N2: WeMos_D1_R1.GND#21, KY-1.C
  N3: WeMos_D1_R1.5V#22, KY-1.power
  N4: WeMos_D1_R1.5V#25, COMPUTER_FAN1.RED
  N5: WeMos_D1_R1.IO34, KY-1.signal
  N6: KY-1.NO, COMPUTER_FAN1.BLACK

custom parts:
  WeMos D1 R32: The D1 R32 is a mini wifi board based on the ESP32.
  Keyes Relay: The Keyes 5V relay module is suitable for SCM development, home appliance control. It uses a 5V~12V TIL control signal which can control DC / AC signal.
  Computer fan: This is a 5V computer fan
