# Fritzing sketch multisensor_wemosD1R32_LCD_pushbutton (saved by Fritzing 0.9.3b)
breadboards: 1

parts:
  Display2 = LCD screen 16x2 I2C [part_number=101290]
  WeMos_D1_R1 = WeMos D1 R32
  R16 = Resistor [tolerance=±5% resistance=3.3k package="1206 [SMD]"]
  SW5 = Pushbutton [package=THT]

nets:
  N1: Display2.GND, WeMos_D1_R1.GND#15
  N2: Display2.VCC, WeMos_D1_R1.5V#25
  N3: Display2.SDA, WeMos_D1_R1.SDA
  N4: Display2.SCL, WeMos_D1_R1.SCL
  N5: WeMos_D1_R1.GND#21, SW5.leg0
  N6: WeMos_D1_R1.5V#22, R16.Pin_0
  N7: R16.Pin_1, SW5.leg1

custom parts:
  WeMos D1 R32: The D1 R32 is a mini wifi board based on the ESP32.
