# Fritzing sketch multisensor_wemosD1R32_LCD_pushbutton_modules (saved by Fritzing 0.9.3b)

parts:
  Display2 = LCD screen 16x2 I2C [part_number=101290]
  WeMos_D1_R32_Shield1 = WeMos D1 R32 with Arduino Sensor Shield v5
  Part1 = KY-004 Key Switch Module [package="Breakout board"]

nets:
  N1: Display2.GND, WeMos_D1_R32_Shield1.GND#79
  N2: Display2.VCC, WeMos_D1_R32_Shield1.5V#80
  N3: Display2.SDA, WeMos_D1_R32_Shield1.SDA
  N4: Display2.SCL, WeMos_D1_R32_Shield1.SCL
  N5: WeMos_D1_R32_Shield1.D2, Part1.S
  N6: WeMos_D1_R32_Shield1.GND#23, Part1.-
  N7: WeMos_D1_R32_Shield1.5V#46, Part1.Vin

custom parts:
  WeMos D1 R32 with Arduino Sensor Shield v5: The D1 R32 is a mini wifi board based on the ESP32 with an Arduino Sensor Shield v5
  KY-004 Key Switch Module: Arduino Key Switch Module Keyes KY-004 is a push button that will output a high signal when pressed.
