# Fritzing sketch multisensor_wemosD1R32_LDR (saved by Fritzing 0.9.3b)
breadboards: 1

parts:
  WeMos_D1_R1 = WeMos D1 R32
  LDR_A1 = Photocell (LDR) [package=THT]
  R9 = Resistor [tolerance=±5% resistance=3.3k package="1206 [SMD]"]

nets:
  N1: WeMos_D1_R1.GND, LDR_A1.pin_0
  N2: WeMos_D1_R1.5V, R9.Pin_0
  N3: WeMos_D1_R1.IO4, LDR_A1.pin_1, R9.Pin_1

custom parts:
  WeMos D1 R32: The D1 R32 is a mini wifi board based on the ESP32.
