# Fritzing sketch multisensor_wemosD1R32_LEDs (saved by Fritzing 0.9.3b)
breadboards: 1

parts:
  WeMos_D1_R1 = WeMos D1 R32
  LED2_D12 = smd LED [color="Red (633nm)" package="0805 [SMD]"]
  LED1_D13 = smd LED [color="Blue (430nm)" package="0805 [SMD]"]
  R7 = Resistor [tolerance=±5% resistance=3.3k package="1206 [SMD]"]
  R8 = Resistor [tolerance=±5% resistance=3.3k package="1206 [SMD]"]

nets:
  N1: WeMos_D1_R1.IO19, R8.Pin_0
  N2: WeMos_D1_R1.IO18, R7.Pin_0
  N3: WeMos_D1_R1.GND, LED2_D12.cathode, LED1_D13.cathode
  N4: LED2_D12.anode, R8.Pin_1
  N5: LED1_D13.anode, R7.Pin_1

custom parts:
  WeMos D1 R32: The D1 R32 is a mini wifi board based on the ESP32.
