# Fritzing sketch multisensor_wemosD1R32_Moist (saved by Fritzing 0.9.3b)

parts:
  WeMos_D1_R1 = WeMos D1 R32
  Componente1 = FC-28 Soil Hygrometer Module - Probe
  Componente2 = FC-28 Soil Hygrometer Module

nets:
  GND: WeMos_D1_R1.GND, Componente2.GND
  5V: WeMos_D1_R1.5V, Componente2.VCC
  N1: WeMos_D1_R1.IO34, Componente2.AO
  N2: Componente1.POS, Componente2.POS
  N3: Componente1.NEG, Componente2.NEG

custom parts:
  WeMos D1 R32: The D1 R32 is a mini wifi board based on the ESP32.
  FC-28 Soil Hygrometer Module - Probe: The FC-28 is a soil hygrometer module that uses the Texas Instruments LM393 comparator chip to provide an analog measurement of soil humidity.
  FC-28 Soil Hygrometer Module: The FC-28 is a soil hygrometer module that uses the Texas Instruments LM393 comparator chip to provide an analog measurement of soil humidity. The digital output is high when soil moisture is over a certain threshold, as determined by adjusting the potentiometer.
