# Fritzing sketch multisensor_wemosD1R32_RGB_IR_buzzer (saved by Fritzing 0.9.3b)
breadboards: 1

parts:
  WeMos_D1_R1 = WeMos D1 R32
  R4 = Resistor [tolerance=±5% resistance=3.3k package="1206 [SMD]"]
  R5 = Resistor [tolerance=±5% resistance=3.3k package="1206 [SMD]"]
  R6 = Resistor [tolerance=±5% resistance=3.3k package="1206 [SMD]"]
  RGB_LED_D9-D11 = RGB LED (com. cathode, rgb) [package="5 mm [THT]"]
  IR2 = TSOP312.., 314.. [package=THT]
  Q5 = NPN-Transistor [package="SOT-23 [SMD]"]
  Buzzer_D9 = Piezo Speaker
  R14 = Resistor [tolerance=±5% resistance=3.3k package="1206 [SMD]"]

nets:
  N1: WeMos_D1_R1.IO16, Q5.0
  N2: WeMos_D1_R1.IO17, IR2.Data
  N3: WeMos_D1_R1.IO23, R5.Pin_0
  GND: WeMos_D1_R1.GND, RGB_LED_D9-D11.common_cathode, IR2.GND, Buzzer_D9.pin1
  N4: WeMos_D1_R1.5V, IR2.Vs, R14.Pin_0
  N5: R4.Pin_1, RGB_LED_D9-D11.red_anode
  N6: R5.Pin_1, RGB_LED_D9-D11.green_anode
  N7: R6.Pin_1, RGB_LED_D9-D11.blue_anode
  N8: Q5.2, Buzzer_D9.pin2
  N9: Q5.1, R14.Pin_1

custom parts:
  WeMos D1 R32: The D1 R32 is a mini wifi board based on the ESP32.
  Piezo Speaker: Piezo
