# Fritzing sketch multisensor_wemosD1R32_RGB_IR_buzzer_modules (saved by Fritzing 0.9.3b)

parts:
  Part2 = KY-016 RGB Full Color LED Module [package="Breakout board"]
  WeMos_D1_R32_Shield1 = WeMos D1 R32 with Arduino Sensor Shield v5
  Part3 = KY-022 Infrared Receiver Module [package="Breakout board"]
  Part4 = KY-006 Passive Buzzer Module [package="Breakout board"]

nets:
  N1: Part2.-, WeMos_D1_R32_Shield1.GND#32
  N2: Part2.R, WeMos_D1_R32_Shield1.D9
  N3: Part2.G, WeMos_D1_R32_Shield1.D11
  N4: Part2.B, WeMos_D1_R32_Shield1.D10
  N5: WeMos_D1_R32_Shield1.D5, Part4.S
  N6: WeMos_D1_R32_Shield1.D6, Part3.S
  N7: WeMos_D1_R32_Shield1.GND#25, Part4.-
  N8: WeMos_D1_R32_Shield1.GND#27, Part3.-
  N9: WeMos_D1_R32_Shield1.5V#48, Part4.+5V
  N10: WeMos_D1_R32_Shield1.5V#49, Part3.Vin

custom parts:
  KY-016 RGB Full Color LED Module: KY-016 Arduino full color 5mm RGB LED, different colors can be obtained by mixing the three primary colors.
  WeMos D1 R32 with Arduino Sensor Shield v5: The D1 R32 is a mini wifi board based on the ESP32 with an Arduino Sensor Shield v5
  KY-022 Infrared Receiver Module: Arduino IR receiver module KY-022, reacts to 38kHz infrared light.
  KY-006 Passive Buzzer Module: Passive Piezoelectric Buzzer Module Keyes KY-006, it can produce a range of sound tones depending on the input frequency.
