# Fritzing sketch multisensor_wemosD1R32_RGB_ldr (saved by Fritzing 0.9.3b)
breadboards: 1

parts:
  WeMos_D1_R1 = WeMos D1 R32
  R4 = Resistor [tolerance=±5% resistance=3.3k package="1206 [SMD]"]
  R5 = Resistor [tolerance=±5% resistance=3.3k package="1206 [SMD]"]
  R6 = Resistor [tolerance=±5% resistance=3.3k package="1206 [SMD]"]
  RGB_LED_D9-D11 = RGB LED (com. cathode, rgb) [package="5 mm [THT]"]
  LDR_A3 = Photocell (LDR) [package=THT]
  R12 = Resistor [tolerance=±5% resistance=3.3k package="1206 [SMD]"]

nets:
  N1: WeMos_D1_R1.IO23, R5.Pin_0
  N2: WeMos_D1_R1.GND, RGB_LED_D9-D11.common_cathode, LDR_A3.pin_0
  N3: WeMos_D1_R1.5V, R12.Pin_1
  N4: WeMos_D1_R1.IO4, LDR_A3.pin_1, R12.Pin_0
  N5: R4.Pin_1, RGB_LED_D9-D11.red_anode
  N6: R5.Pin_1, RGB_LED_D9-D11.green_anode
  N7: R6.Pin_1, RGB_LED_D9-D11.blue_anode

custom parts:
  WeMos D1 R32: The D1 R32 is a mini wifi board based on the ESP32.
