# Fritzing sketch multisensor_wemosD1R32_RGB_ldr_modules (saved by Fritzing 0.9.3b)

parts:
  Part2 = KY-016 RGB Full Color LED Module [package="Breakout board"]
  WeMos_D1_R32_Shield1 = WeMos D1 R32 with Arduino Sensor Shield v5
  R2 = Photocell (LDR) [package=THT]

nets:
  N1: Part2.-, WeMos_D1_R32_Shield1.GND#32
  N2: Part2.R, WeMos_D1_R32_Shield1.D9
  N3: Part2.G, WeMos_D1_R32_Shield1.D11
  N4: Part2.B, WeMos_D1_R32_Shield1.D10
  N5: WeMos_D1_R32_Shield1.A0, R2.S
  N6: WeMos_D1_R32_Shield1.GND#65, R2.-
  N7: WeMos_D1_R32_Shield1.5V, R2.+

custom parts:
  KY-016 RGB Full Color LED Module: KY-016 Arduino full color 5mm RGB LED, different colors can be obtained by mixing the three primary colors.
  WeMos D1 R32 with Arduino Sensor Shield v5: The D1 R32 is a mini wifi board based on the ESP32 with an Arduino Sensor Shield v5
  Photocell (LDR): A generic light dependent resistor (LDR)
