# Fritzing sketch multisensor_wemosD1R32_RGB_pushbutton_buzzer (saved by Fritzing 0.9.3b)
breadboards: 1

parts:
  WeMos_D1_R1 = WeMos D1 R32
  SW2 = Pushbutton [package=THT]
  R11 = Resistor [tolerance=±5% resistance=3.3k package="1206 [SMD]"]
  Q3 = NPN-Transistor [package="SOT-23 [SMD]"]
  Buzzer_D7 = Piezo Speaker
  R12 = Resistor [tolerance=±5% resistance=3.3k package="1206 [SMD]"]
  LED2 = RGB LED (com. cathode, rgb) [package="5 mm [THT]"]
  R13 = Resistor [tolerance=±5% resistance=3.3k package="1206 [SMD]"]
  R14 = Resistor [tolerance=±5% resistance=3.3k package="1206 [SMD]"]
  R15 = Resistor [tolerance=±5% resistance=3.3k package="1206 [SMD]"]

nets:
  N1: WeMos_D1_R1.IO26, SW2.leg1, R11.Pin_1
  N2: WeMos_D1_R1.IO16, Q3.0
  N3: WeMos_D1_R1.IO13, R13.Pin_1
  N4: WeMos_D1_R1.IO5, R14.Pin_0
  N5: WeMos_D1_R1.IO23, R15.Pin_0
  N6: WeMos_D1_R1.GND, SW2.leg0, Buzzer_D7.pin1, LED2.common_cathode
  N7: WeMos_D1_R1.5V, R11.Pin_0, Q3.1, R12.Pin_1
  N8: Q3.2, Buzzer_D7.pin2
  N9: LED2.red_anode, R13.Pin_0
  N10: LED2.green_anode, R15.Pin_1
  N11: LED2.blue_anode, R14.Pin_1

custom parts:
  WeMos D1 R32: The D1 R32 is a mini wifi board based on the ESP32.
  Piezo Speaker: Piezo
