# Fritzing sketch multisensor_wemosD1R32_bmp180 (saved by Fritzing 0.9.3b)

parts:
  WeMos_D1_R1 = WeMos D1 R32
  Componente1 = Adafruit BMP180

nets:
  GND: WeMos_D1_R1.GND, Componente1.GND
  5V: WeMos_D1_R1.5V, Componente1.+3V3
  N1: WeMos_D1_R1.SDA, Componente1.SDA
  N2: WeMos_D1_R1.SCL, Componente1.SCL

custom parts:
  WeMos D1 R32: The D1 R32 is a mini wifi board based on the ESP32.
  Adafruit BMP180: This precision sensor from Bosch is the best low-cost sensing solution for measuring barometric pressure and temperature. Because pressure changes with altitude you can also use it as an altimeter! The sensor is soldered onto a PCB with a 3.3V regulator, I2C level shifter and pull-up resistors on the I2C pins. The BMP180 is the next-generation of sensors from Bosch, and replaces the BMP085.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
