# Fritzing sketch multisensor_wemosD1R32_buzzer (saved by Fritzing 0.9.3b)
breadboards: 1

parts:
  WeMos_D1_R1 = WeMos D1 R32
  Buzzer_D5 = Piezo Speaker
  Q1 = NPN-Transistor [package="SOT-23 [SMD]"]
  R3 = Resistor [tolerance=±5% resistance=3.3k package="1206 [SMD]"]

nets:
  N1: WeMos_D1_R1.IO16, Q1.0
  N2: WeMos_D1_R1.GND, Buzzer_D5.pin1
  N3: WeMos_D1_R1.5V, R3.Pin_0
  N4: Buzzer_D5.pin2, Q1.2
  N5: Q1.1, R3.Pin_1

custom parts:
  WeMos D1 R32: The D1 R32 is a mini wifi board based on the ESP32.
  Piezo Speaker: Piezo
