# Fritzing sketch multisensor_wemosD1R32_dht11 (saved by Fritzing 0.9.3b)
breadboards: 1

parts:
  WeMos_D1_R1 = WeMos D1 R32
  DHT11_D4 = DHT11 Humitidy and Temperature Sensor

nets:
  N1: WeMos_D1_R1.IO7, DHT11_D4.DATA
  GND: WeMos_D1_R1.GND, DHT11_D4.GND
  5V: WeMos_D1_R1.5V, DHT11_D4.VDD

custom parts:
  WeMos D1 R32: The D1 R32 is a mini wifi board based on the ESP32.
  DHT11 Humitidy and Temperature Sensor: DHT11 Humidity and Temperature Sensor
