# Fritzing sketch multisensor_wemosD1R32_gas (saved by Fritzing 0.9.3b)

parts:
  WeMos_D1_R1 = WeMos D1 R32  # not connected
  U1 = MultiSensor Shield
  Componente2 = MQ-3 breakout

nets:
  N1: U1.D8, Componente2.DO
  GND: U1.GND, Componente2.GND
  VCC: U1.VCC, Componente2.VCC
  N2: U1.A3, Componente2.AO

custom parts:
  WeMos D1 R32: The D1 R32 is a mini wifi board based on the ESP32.
  MultiSensor Shield: MultiSensor Shield for Arduino compatible boards
  MQ-3 breakout: Alcohol sensor is capable of detecting alcohol (ethanol) particles on itself and gives the information in digital form back to us to manipulate with it. SKU:101251 • Voltage: 5V DC • Power: max 750mW • Measurement range: 0.04-4mg/L
