# Fritzing sketch multisensor_wemosD1R32_gas_LED_pushbutton_buzzer (saved by Fritzing 0.9.3b)
breadboards: 1

parts:
  WeMos_D1_R1 = WeMos D1 R32
  SW2 = Pushbutton [package=THT]
  R11 = Resistor [tolerance=±5% resistance=3.3k package="1206 [SMD]"]
  Q3 = NPN-Transistor [package="SOT-23 [SMD]"]
  Buzzer_D7 = Piezo Speaker
  R12 = Resistor [tolerance=±5% resistance=3.3k package="1206 [SMD]"]
  R14 = Resistor [tolerance=±5% resistance=3.3k package="1206 [SMD]"]
  LED2_D14 = smd LED [color="Red (633nm)" package="0805 [SMD]"]
  Componente7 = MQ-3 breakout

nets:
  N1: WeMos_D1_R1.IO26, SW2.leg1, R11.Pin_1
  N2: WeMos_D1_R1.IO16, Q3.0
  N3: WeMos_D1_R1.IO12, Componente7.DO
  N4: WeMos_D1_R1.IO19, LED2_D14.anode
  GND: WeMos_D1_R1.GND, SW2.leg0, Buzzer_D7.pin1, R14.Pin_0, Componente7.GND
  5V: WeMos_D1_R1.5V, R11.Pin_0, Q3.1, R12.Pin_1, Componente7.VCC
  N5: WeMos_D1_R1.IO34, Componente7.AO
  N6: Q3.2, Buzzer_D7.pin2
  N7: R14.Pin_1, LED2_D14.cathode

custom parts:
  WeMos D1 R32: The D1 R32 is a mini wifi board based on the ESP32.
  Piezo Speaker: Piezo
  MQ-3 breakout: Alcohol sensor is capable of detecting alcohol (ethanol) particles on itself and gives the information in digital form back to us to manipulate with it. SKU:101251 • Voltage: 5V DC • Power: max 750mW • Measurement range: 0.04-4mg/L
