# Fritzing sketch multisensor_wemosD1R32_gas_RGB_pushbutton_buzzer_modules (saved by Fritzing 0.9.3b)

parts:
  Part1 = KY-004 Key Switch Module [package="Breakout board"]
  WeMos_D1_R32_Shield1 = WeMos D1 R32 with Arduino Sensor Shield v5
  Part5 = KY-006 Passive Buzzer Module [package="Breakout board"]
  Part6 = KY-016 RGB Full Color LED Module [package="Breakout board"]
  Componente1 = MQ-3 breakout

nets:
  N1: Part1.S, WeMos_D1_R32_Shield1.D2
  N2: Part1.Vin, WeMos_D1_R32_Shield1.5V#45
  N3: Part1.-, WeMos_D1_R32_Shield1.GND#22
  N4: WeMos_D1_R32_Shield1.D5, Part5.S
  N5: WeMos_D1_R32_Shield1.D8, Componente1.DO
  N6: WeMos_D1_R32_Shield1.D9, Part6.R
  N7: WeMos_D1_R32_Shield1.D10, Part6.B
  N8: WeMos_D1_R32_Shield1.D11, Part6.G
  N9: WeMos_D1_R32_Shield1.GND#25, Part5.-
  N10: WeMos_D1_R32_Shield1.GND#30, Part6.-
  N11: WeMos_D1_R32_Shield1.5V#48, Part5.+5V
  N12: WeMos_D1_R32_Shield1.A3, Componente1.AO
  N13: WeMos_D1_R32_Shield1.GND#68, Componente1.GND
  N14: WeMos_D1_R32_Shield1.5V#74, Componente1.VCC

custom parts:
  KY-004 Key Switch Module: Arduino Key Switch Module Keyes KY-004 is a push button that will output a high signal when pressed.
  WeMos D1 R32 with Arduino Sensor Shield v5: The D1 R32 is a mini wifi board based on the ESP32 with an Arduino Sensor Shield v5
  KY-006 Passive Buzzer Module: Passive Piezoelectric Buzzer Module Keyes KY-006, it can produce a range of sound tones depending on the input frequency.
  KY-016 RGB Full Color LED Module: KY-016 Arduino full color 5mm RGB LED, different colors can be obtained by mixing the three primary colors.
  MQ-3 breakout: Alcohol sensor is capable of detecting alcohol (ethanol) particles on itself and gives the information in digital form back to us to manipulate with it. SKU:101251 • Voltage: 5V DC • Power: max 750mW • Measurement range: 0.04-4mg/L
