# Fritzing sketch multisensor_wemosD1R32_lm35 (saved by Fritzing 0.9.3b)
breadboards: 1

parts:
  WeMos_D1_R1 = WeMos D1 R32
  LM35_A2 = LM35 Temperature Sensor [package="TO92 [THT]"]

nets:
  GND: WeMos_D1_R1.GND, LM35_A2.GND
  N1: WeMos_D1_R1.5V, LM35_A2.+Vs
  N2: WeMos_D1_R1.IO38, LM35_A2.Vout

custom parts:
  WeMos D1 R32: The D1 R32 is a mini wifi board based on the ESP32.
