# Fritzing sketch multisensor_wemosD1R32_oled (saved by Fritzing 0.9.3b)

parts:
  WeMos_D1_R1 = WeMos D1 R32
  Grove1 = Grove OLED 128x96

nets:
  GND: WeMos_D1_R1.GND, Grove1.GND
  5V: WeMos_D1_R1.5V, Grove1.VCC
  N1: WeMos_D1_R1.SDA, Grove1.SDA
  N2: WeMos_D1_R1.SCL, Grove1.SCL

custom parts:
  WeMos D1 R32: The D1 R32 is a mini wifi board based on the ESP32.
