# Fritzing sketch multisensor_wemosD1R32_pot (saved by Fritzing 0.9.3b)
breadboards: 1

parts:
  WeMos_D1_R1 = WeMos D1 R32
  Rotation_A0 = POT [package=alps_pot]

nets:
  N1: WeMos_D1_R1.GND, Rotation_A0.A
  N2: WeMos_D1_R1.5V, Rotation_A0.E
  N3: WeMos_D1_R1.IO2, Rotation_A0.S

custom parts:
  WeMos D1 R32: The D1 R32 is a mini wifi board based on the ESP32.
