# Fritzing sketch multisensor_wemosD1R32_pot_LEDs_buzzer (saved by Fritzing 0.9.3b)
breadboards: 1

parts:
  WeMos_D1_R1 = WeMos D1 R32
  R9 = Resistor [tolerance=±5% resistance=3.3k package="1206 [SMD]"]
  R10 = Resistor [tolerance=±5% resistance=3.3k package="1206 [SMD]"]
  LED1_D14 = smd LED [color="Blue (430nm)" package="0805 [SMD]"]
  LED2_D13 = smd LED [color="Red (633nm)" package="0805 [SMD]"]
  SW2 = Pushbutton [package=THT]
  R11 = Resistor [tolerance=±5% resistance=3.3k package="1206 [SMD]"]
  Q3 = NPN-Transistor [package="SOT-23 [SMD]"]
  Buzzer_D7 = Piezo Speaker
  R12 = Resistor [tolerance=±5% resistance=3.3k package="1206 [SMD]"]

nets:
  N1: WeMos_D1_R1.IO26, SW2.leg1, R11.Pin_1
  N2: WeMos_D1_R1.IO16, Q3.0
  N3: WeMos_D1_R1.IO19, R9.Pin_0
  N4: WeMos_D1_R1.IO18, R10.Pin_0
  N5: WeMos_D1_R1.GND, LED1_D14.cathode, LED2_D13.cathode, SW2.leg0, Buzzer_D7.pin1
  N6: WeMos_D1_R1.5V, R11.Pin_0, R12.Pin_0
  N7: R9.Pin_1, LED2_D13.anode
  N8: R10.Pin_1, LED1_D14.anode
  N9: Q3.2, Buzzer_D7.pin2
  N10: Q3.1, R12.Pin_1

custom parts:
  WeMos D1 R32: The D1 R32 is a mini wifi board based on the ESP32.
  Piezo Speaker: Piezo
