# Fritzing sketch multisensor_wemosD1R32_pot_LEDs_ldr_lm35 (saved by Fritzing 0.9.3b)
breadboards: 1

parts:
  WeMos_D1_R1 = WeMos D1 R32
  Rotation_A0 = POT [package=alps_pot]
  R9 = Resistor [tolerance=±5% resistance=3.3k package="1206 [SMD]"]
  R10 = Resistor [tolerance=±5% resistance=3.3k package="1206 [SMD]"]
  LED1_D14 = smd LED [color="Blue (430nm)" package="0805 [SMD]"]
  LED2_D13 = smd LED [color="Red (633nm)" package="0805 [SMD]"]
  R11 = Resistor [tolerance=±5% resistance=3.3k package="1206 [SMD]"]
  LDR_A2 = Photocell (LDR) [package=THT]
  LM35_A3 = LM35 Temperature Sensor [package="TO92 [THT]"]

nets:
  N1: WeMos_D1_R1.IO19, R9.Pin_0
  N2: WeMos_D1_R1.IO18, R10.Pin_0
  GND: WeMos_D1_R1.GND, Rotation_A0.A, LED1_D14.cathode, LED2_D13.cathode, LDR_A2.pin_0, LM35_A3.GND
  N3: WeMos_D1_R1.5V, Rotation_A0.E, R11.Pin_1, LM35_A3.+Vs
  N4: WeMos_D1_R1.IO2, Rotation_A0.S
  N5: WeMos_D1_R1.IO4, R11.Pin_0, LDR_A2.pin_1
  N6: WeMos_D1_R1.IO38, LM35_A3.Vout
  N7: R9.Pin_1, LED2_D13.anode
  N8: R10.Pin_1, LED1_D14.anode

custom parts:
  WeMos D1 R32: The D1 R32 is a mini wifi board based on the ESP32.
