# Fritzing sketch multisensor_wemosD1R32_pot_LEDs_ldr_lm35_modules (saved by Fritzing 0.9.3b)

parts:
  Part2 = KY-016 RGB Full Color LED Module [package="Breakout board"]
  Part3 = Potentiometer module [package="Breakout board"]
  WeMos_D1_R32_Shield1 = WeMos D1 R32 with Arduino Sensor Shield v5
  R1 = Photocell (LDR) [package=THT]
  Part5 = LM35 [package="Breakout board"]

nets:
  N1: Part2.-, WeMos_D1_R32_Shield1.GND#40
  N2: Part2.R, WeMos_D1_R32_Shield1.D12
  N3: Part2.B, WeMos_D1_R32_Shield1.D13
  N4: Part3.S, WeMos_D1_R32_Shield1.A0
  N5: Part3.Vin, WeMos_D1_R32_Shield1.5V#71
  N6: Part3.-, WeMos_D1_R32_Shield1.GND#65
  N7: WeMos_D1_R32_Shield1.A1, R1.S
  N8: WeMos_D1_R32_Shield1.A2, Part5.S
  N9: WeMos_D1_R32_Shield1.GND#66, R1.-
  N10: WeMos_D1_R32_Shield1.GND#67, Part5.-
  N11: WeMos_D1_R32_Shield1.5V#72, R1.+
  N12: WeMos_D1_R32_Shield1.5V#73, Part5.Vin

custom parts:
  KY-016 RGB Full Color LED Module: KY-016 Arduino full color 5mm RGB LED, different colors can be obtained by mixing the three primary colors.
  Potentiometer module: A potentiometer module
  WeMos D1 R32 with Arduino Sensor Shield v5: The D1 R32 is a mini wifi board based on the ESP32 with an Arduino Sensor Shield v5
  Photocell (LDR): A generic light dependent resistor (LDR)
  LM35: Arduino Temperature Sensor Module LM35
