# Fritzing sketch multisensor_wemosD1R32_pot_LEDs_pushbuttons (saved by Fritzing 0.9.3b)
breadboards: 1

parts:
  WeMos_D1_R1 = WeMos D1 R32
  Rotation_A0 = POT [package=alps_pot]
  R9 = Resistor [tolerance=±5% resistance=3.3k package="1206 [SMD]"]
  R10 = Resistor [tolerance=±5% resistance=3.3k package="1206 [SMD]"]
  LED1_D14 = smd LED [color="Blue (430nm)" package="0805 [SMD]"]
  LED2_D13 = smd LED [color="Red (633nm)" package="0805 [SMD]"]
  SW2 = Pushbutton [package=THT]
  R11 = Resistor [tolerance=±5% resistance=3.3k package="1206 [SMD]"]
  SW3 = Pushbutton [package=THT]
  R12 = Resistor [tolerance=±5% resistance=3.3k package="1206 [SMD]"]

nets:
  N1: WeMos_D1_R1.IO26, SW2.leg1, R11.Pin_1
  N2: WeMos_D1_R1.IO25, SW3.leg1, R12.Pin_1
  N3: WeMos_D1_R1.IO19, R9.Pin_0
  N4: WeMos_D1_R1.IO18, R10.Pin_0
  N5: WeMos_D1_R1.GND, Rotation_A0.A, LED1_D14.cathode, LED2_D13.cathode, SW2.leg0, SW3.leg0
  N6: WeMos_D1_R1.5V, Rotation_A0.E, R11.Pin_0, R12.Pin_0
  N7: WeMos_D1_R1.IO2, Rotation_A0.S
  N8: R9.Pin_1, LED2_D13.anode
  N9: R10.Pin_1, LED1_D14.anode

custom parts:
  WeMos D1 R32: The D1 R32 is a mini wifi board based on the ESP32.
