# Fritzing sketch multisensor_wemosD1R32_pot_LEDs_pushbuttons_modules (saved by Fritzing 0.9.3b)

parts:
  Part1 = KY-004 Key Switch Module [package="Breakout board"]
  Part2 = KY-016 RGB Full Color LED Module [package="Breakout board"]
  Part3 = Potentiometer module [package="Breakout board"]
  WeMos_D1_R32_Shield1 = WeMos D1 R32 with Arduino Sensor Shield v5
  Part4 = KY-004 Key Switch Module [package="Breakout board"]

nets:
  N1: Part1.S, WeMos_D1_R32_Shield1.D2
  N2: Part1.Vin, WeMos_D1_R32_Shield1.5V#45
  N3: Part1.-, WeMos_D1_R32_Shield1.GND#22
  N4: Part2.-, WeMos_D1_R32_Shield1.GND#40
  N5: Part2.R, WeMos_D1_R32_Shield1.D12
  N6: Part2.B, WeMos_D1_R32_Shield1.D13
  N7: Part3.S, WeMos_D1_R32_Shield1.A0
  N8: Part3.Vin, WeMos_D1_R32_Shield1.5V#71
  N9: Part3.-, WeMos_D1_R32_Shield1.GND#65
  N10: WeMos_D1_R32_Shield1.D3, Part4.S
  N11: WeMos_D1_R32_Shield1.GND#23, Part4.-
  N12: WeMos_D1_R32_Shield1.5V#46, Part4.Vin

custom parts:
  KY-004 Key Switch Module: Arduino Key Switch Module Keyes KY-004 is a push button that will output a high signal when pressed.
  KY-016 RGB Full Color LED Module: KY-016 Arduino full color 5mm RGB LED, different colors can be obtained by mixing the three primary colors.
  Potentiometer module: A potentiometer module
  WeMos D1 R32 with Arduino Sensor Shield v5: The D1 R32 is a mini wifi board based on the ESP32 with an Arduino Sensor Shield v5
