# Fritzing sketch multisensor_wemosD1R32_pot_modules (saved by Fritzing 0.9.3b)

parts:
  Part3 = Potentiometer module [package="Breakout board"]
  WeMos_D1_R32_Shield1 = WeMos D1 R32 with Arduino Sensor Shield v5

nets:
  N1: Part3.S, WeMos_D1_R32_Shield1.A0
  VIN: Part3.Vin, WeMos_D1_R32_Shield1.5V
  N2: Part3.-, WeMos_D1_R32_Shield1.GND

custom parts:
  Potentiometer module: A potentiometer module
  WeMos D1 R32 with Arduino Sensor Shield v5: The D1 R32 is a mini wifi board based on the ESP32 with an Arduino Sensor Shield v5
