# Fritzing sketch multisensor_wemosD1R32_pushbuttons (saved by Fritzing 0.9.3b)
breadboards: 1

parts:
  R1 = Resistor [tolerance=±5% resistance=3.3k package="1206 [SMD]"]
  SW1 = Pushbutton [package=THT]
  WeMos_D1_R1 = WeMos D1 R32
  SW2 = Pushbutton [package=THT]
  R2 = Resistor [tolerance=±5% resistance=3.3k package="1206 [SMD]"]

nets:
  N1: R1.Pin_0, WeMos_D1_R1.5V, R2.Pin_0
  N2: R1.Pin_1, SW1.leg1, WeMos_D1_R1.IO26
  N3: SW1.leg0, WeMos_D1_R1.GND, SW2.leg0
  N4: WeMos_D1_R1.IO25, SW2.leg1, R2.Pin_1

custom parts:
  WeMos D1 R32: The D1 R32 is a mini wifi board based on the ESP32.
