# Fritzing sketch multisensor_wemosD1R32_pushbuttons_buzzer (saved by Fritzing 0.9.3b)
breadboards: 1

parts:
  WeMos_D1_R1 = WeMos D1 R32
  R10 = Resistor [tolerance=±5% resistance=3.3k package="1206 [SMD]"]
  SW2 = Pushbutton [package=THT]
  R11 = Resistor [tolerance=±5% resistance=3.3k package="1206 [SMD]"]
  Q3 = NPN-Transistor [package="SOT-23 [SMD]"]
  Buzzer_D7 = Piezo Speaker
  R12 = Resistor [tolerance=±5% resistance=3.3k package="1206 [SMD]"]
  SW3 = Pushbutton [package=THT]

nets:
  N1: WeMos_D1_R1.IO26, SW2.leg1, R11.Pin_1
  N2: WeMos_D1_R1.IO25, R10.Pin_0, SW3.leg1
  N3: WeMos_D1_R1.IO16, Q3.0
  N4: WeMos_D1_R1.GND, SW2.leg0, Buzzer_D7.pin1, SW3.leg0
  N5: WeMos_D1_R1.5V, R10.Pin_1, R11.Pin_0, Q3.1, R12.Pin_1
  N6: Q3.2, Buzzer_D7.pin2

custom parts:
  WeMos D1 R32: The D1 R32 is a mini wifi board based on the ESP32.
  Piezo Speaker: Piezo
