# Fritzing sketch multisensor_wemosD1R32_pushbuttons_buzzer_modules (saved by Fritzing 0.9.3b)

parts:
  Part1 = KY-004 Key Switch Module [package="Breakout board"]
  WeMos_D1_R32_Shield1 = WeMos D1 R32 with Arduino Sensor Shield v5
  Part4 = KY-004 Key Switch Module [package="Breakout board"]
  Part5 = KY-006 Passive Buzzer Module [package="Breakout board"]

nets:
  N1: Part1.S, WeMos_D1_R32_Shield1.D2
  N2: Part1.Vin, WeMos_D1_R32_Shield1.5V#45
  N3: Part1.-, WeMos_D1_R32_Shield1.GND#22
  N4: WeMos_D1_R32_Shield1.D3, Part4.S
  N5: WeMos_D1_R32_Shield1.D5, Part5.S
  N6: WeMos_D1_R32_Shield1.GND#23, Part4.-
  N7: WeMos_D1_R32_Shield1.GND#25, Part5.-
  N8: WeMos_D1_R32_Shield1.5V#46, Part4.Vin
  N9: WeMos_D1_R32_Shield1.5V#48, Part5.+5V

custom parts:
  KY-004 Key Switch Module: Arduino Key Switch Module Keyes KY-004 is a push button that will output a high signal when pressed.
  WeMos D1 R32 with Arduino Sensor Shield v5: The D1 R32 is a mini wifi board based on the ESP32 with an Arduino Sensor Shield v5
  KY-006 Passive Buzzer Module: Passive Piezoelectric Buzzer Module Keyes KY-006, it can produce a range of sound tones depending on the input frequency.
