# Fritzing sketch multisensor_wemosD1R32_servo_relay_fan_pot_pushbutton (saved by Fritzing 0.9.3b)
breadboards: 1

parts:
  WeMos_D1_R1 = WeMos D1 R32
  Rotation_A0 = POT [package=alps_pot]
  SW2 = Pushbutton [package=THT]
  R11 = Resistor [tolerance=±5% resistance=3.3k package="1206 [SMD]"]
  J1 = Basic Servo
  KY-1 = Keyes Relay [package=THT]
  COMPUTER_FAN1 = Computer fan

nets:
  N1: WeMos_D1_R1.IO26, SW2.leg1, R11.Pin_1
  N2: WeMos_D1_R1.IO14, KY-1.signal
  N3: WeMos_D1_R1.IO12, J1.pulse
  GND: WeMos_D1_R1.GND, Rotation_A0.A, SW2.leg0, J1.gnd, KY-1.ground, COMPUTER_FAN1.BLACK
  5V: WeMos_D1_R1.5V, Rotation_A0.E, R11.Pin_0, J1.vcc, KY-1.power, KY-1.C
  N4: WeMos_D1_R1.IO2, Rotation_A0.S
  N5: KY-1.NO, COMPUTER_FAN1.RED

custom parts:
  WeMos D1 R32: The D1 R32 is a mini wifi board based on the ESP32.
  Keyes Relay: The Keyes 5V relay module is suitable for SCM development, home appliance control. It uses a 5V~12V TIL control signal which can control DC / AC signal.
  Computer fan: This is a 5V computer fan
