# Fritzing sketch multisensor_wemosD1R32_servo_relay_fan_pot_pushbutton_modules (saved by Fritzing 0.9.3b)

parts:
  Part1 = KY-004 Key Switch Module [package="Breakout board"]
  Part3 = Potentiometer module [package="Breakout board"]
  WeMos_D1_R32_Shield1 = WeMos D1 R32 with Arduino Sensor Shield v5
  KY-2 = Keyes Relay [package=THT]
  COMPUTER_FAN2 = Computer fan
  J2 = Basic Servo

nets:
  N1: Part1.S, WeMos_D1_R32_Shield1.D2
  N2: Part1.Vin, WeMos_D1_R32_Shield1.5V#45
  N3: Part1.-, WeMos_D1_R32_Shield1.GND#22
  N4: Part3.S, WeMos_D1_R32_Shield1.A0
  N5: Part3.Vin, WeMos_D1_R32_Shield1.5V#71
  N6: Part3.-, WeMos_D1_R32_Shield1.GND#65
  N7: WeMos_D1_R32_Shield1.D8, J2.pulse
  N8: WeMos_D1_R32_Shield1.GND#28, KY-2.ground
  N9: WeMos_D1_R32_Shield1.GND#29, J2.gnd
  N10: WeMos_D1_R32_Shield1.GND#42, COMPUTER_FAN2.BLACK
  N11: WeMos_D1_R32_Shield1.5V#50, KY-2.power
  N12: WeMos_D1_R32_Shield1.5V#51, J2.vcc
  N13: WeMos_D1_R32_Shield1.5V#58, KY-2.C
  N14: KY-2.NO, COMPUTER_FAN2.RED

custom parts:
  KY-004 Key Switch Module: Arduino Key Switch Module Keyes KY-004 is a push button that will output a high signal when pressed.
  Potentiometer module: A potentiometer module
  WeMos D1 R32 with Arduino Sensor Shield v5: The D1 R32 is a mini wifi board based on the ESP32 with an Arduino Sensor Shield v5
  Keyes Relay: The Keyes 5V relay module is suitable for SCM development, home appliance control. It uses a 5V~12V TIL control signal which can control DC / AC signal.
  Computer fan: This is a 5V computer fan
