# Fritzing sketch pot_nodemcu_example (saved by Fritzing 0.9.3b)

parts:
  R1 = Trimmer Potentiometer [maximum_resistance=10kΩ package=THT]
  Componente1 = NodeMcu base board

nets:
  N1: R1.leg1, Componente1.3V
  N2: R1.wiper, Componente1.A0
  N3: R1.leg2, Componente1.GND

custom parts:
  NodeMcu base board: ESP8266 WiFi Expansion Board For NodeMCU ESP-12E
