# Fritzing sketch pot_wemosD1R32_example (saved by Fritzing 0.9.3b)

parts:
  R1 = Trimmer Potentiometer [maximum_resistance=10kΩ package=THT]
  WeMos_D1_R32_Shield1 = WeMos D1 R32 with Arduino Sensor Shield v5

nets:
  N1: R1.leg1, WeMos_D1_R32_Shield1.5V
  N2: R1.wiper, WeMos_D1_R32_Shield1.A1
  N3: R1.leg2, WeMos_D1_R32_Shield1.GND

custom parts:
  WeMos D1 R32 with Arduino Sensor Shield v5: The D1 R32 is a mini wifi board based on the ESP32 with an Arduino Sensor Shield v5
