# Fritzing sketch potentiometer (saved by Fritzing 0.9.2b)

parts:
  R2 = TRIMPOT [package=trimpot_pth_s3_lock]
  Parte1 = Arduino Nano (Rev3.0)
  VCC3 = Battery block 9V  # not connected

nets:
  N1: R2.CCW, Parte1.GND
  N2: R2.WIPER, Parte1.A0
  N3: R2.CW, Parte1.5V

custom parts:
  Arduino Nano (Rev3.0): Arduino Nano 3.0 IO expansion board
