# Fritzing sketch pot_motor_example (saved by Fritzing 0.9.3b)
breadboards: 1

parts:
  Componente1 = Arduino Nano Expansion Board (Rev3.0)
  R1 = Trimmer Potentiometer [maximum_resistance=10kΩ package=THT]
  M1 = DC Motor
  Q1 = NPN-Transistor [package="TO92 [THT]"]
  R2 = Resistor [tolerance=±5% resistance=220 package="2512 [SMD]"]

nets:
  N1: Componente1.D3/PWM0, R2.Pin_0
  N2: Componente1.A0, R1.wiper
  N3: Componente1.GND#66, M1.pin_2
  N4: Componente1.GND#68, R1.leg2
  N5: Componente1.5V#95, Q1.C
  N6: Componente1.5V#97, R1.leg1
  N7: M1.pin_1, Q1.E
  N8: Q1.B, R2.Pin_1

custom parts:
  Arduino Nano Expansion Board (Rev3.0): Arduino Nano 3.0 IO expansion board
