# Fritzing sketch red_green_led_button (saved by Fritzing 0.9.3b)

parts:
  Part1 = KY-011 Two Color LED Module [package="Breakout board"]
  Componente1 = Arduino Nano Expansion Board (Rev3.0)
  Part2 = KY-004 Key Switch Module [package="Breakout board"]

nets:
  N1: Part1.S, Componente1.D4
  N2: Part1.Vin, Componente1.D3/PWM0
  N3: Part1.-, Componente1.GND#54
  N4: Componente1.D2, Part2.S
  N5: Componente1.GND#52, Part2.-
  5V: Componente1.5V, Part2.Vin

custom parts:
  KY-011 Two Color LED Module: KEYES KY-011 Two Color LED Module consist of a common cathode 3mm red/green LED.
  Arduino Nano Expansion Board (Rev3.0): Arduino Nano 3.0 IO expansion board
  KY-004 Key Switch Module: Arduino Key Switch Module Keyes KY-004 is a push button that will output a high signal when pressed.
