# Fritzing sketch relay_buttons3_example (saved by Fritzing 0.9.3b)

parts:
  Componente1 = Arduino Nano Expansion Board (Rev3.0)
  M1 = DC Motor
  VCC1 = Battery block 9V
  KY-1 = Keyes Relay [package=THT]
  Part1 = KY-004 Key Switch Module [package="Breakout board"]
  Part2 = KY-004 Key Switch Module [package="Breakout board"]
  Part3 = KY-004 Key Switch Module [package="Breakout board"]
  KY-2 = Keyes Relay [package=THT]
  M2 = DC Motor

nets:
  N1: Componente1.D2, Part1.S
  N2: Componente1.D3/PWM0, Part2.-
  N3: Componente1.D4, Part3.S
  N4: Componente1.D5/PWM1, KY-1.signal
  N5: Componente1.D6/PWM2, KY-2.signal
  N6: Componente1.D12, Componente1.GND#55, KY-1.ground
  N7: Componente1.GND#52, Part1.-
  N8: Componente1.GND#53, Part2.S
  N9: Componente1.GND#54, Part3.-
  N10: Componente1.GND#56, KY-2.ground
  N11: Componente1.GND#64, M2.pin_2
  N12: Componente1.GND#65, M1.pin_2
  N13: Componente1.5V#81, Part1.Vin
  N14: Componente1.5V#82, Part2.Vin
  N15: Componente1.5V#83, Part3.Vin
  N16: Componente1.5V#84, KY-1.power
  N17: Componente1.5V#85, KY-2.power
  N18: M1.pin_1, KY-1.NC
  N19: VCC1.+, KY-1.C, KY-2.C
  N20: KY-2.NC, M2.pin_1

custom parts:
  Arduino Nano Expansion Board (Rev3.0): Arduino Nano 3.0 IO expansion board
  Keyes Relay: The Keyes 5V relay module is suitable for SCM development, home appliance control. It uses a 5V~12V TIL control signal which can control DC / AC signal.
  KY-004 Key Switch Module: Arduino Key Switch Module Keyes KY-004 is a push button that will output a high signal when pressed.
