# Fritzing sketch relay_buttons_led_example (saved by Fritzing 0.9.3b)
breadboards: 1

parts:
  Componente1 = Arduino Nano Expansion Board (Rev3.0)
  S1 = Pushbutton [package="[THT]"]
  M1 = DC Motor
  U2 = RELAY [package=relay-t9a]
  VCC1 = Battery block 9V
  S2 = Pushbutton [package="[THT]"]
  LED1 = LED - 5mm [color="Red (633nm)" package="5 mm [THT]"]  # not connected

nets:
  N1: Componente1.D2, S1.Pin_3, S1.Pin_4
  N2: Componente1.D3/PWM0, S2.Pin_3, S2.Pin_4
  N3: Componente1.D4, U2.COIL1
  N4: Componente1.GND#54, U2.COIL2
  N5: Componente1.GND#66, S1.Pin_1, S1.Pin_2, S2.Pin_1, S2.Pin_2
  N6: M1.pin_1, U2.NC
  N7: M1.pin_2, VCC1.-
  N8: U2.MAIN, VCC1.+

custom parts:
  Arduino Nano Expansion Board (Rev3.0): Arduino Nano 3.0 IO expansion board
