# Fritzing sketch relay_buttons_nano_example (saved by Fritzing 0.9.3b)

parts:
  KY-1 = Keyes Relay [package=THT]
  Part1 = KY-004 Key Switch Module [package="Breakout board"]
  Part2 = KY-004 Key Switch Module [package="Breakout board"]
  Componente2 = Arduino Nano (Rev3.0)
  COMPUTER_FAN1 = Computer fan

nets:
  N1: KY-1.signal, Componente2.D4
  N2: KY-1.power, Componente2.5V#90
  N3: KY-1.ground, Componente2.GND#61
  N4: KY-1.NC, COMPUTER_FAN1.RED
  N5: KY-1.C, Componente2.5V#79
  N6: Part1.S, Componente2.D2
  N7: Part1.Vin, Componente2.5V#92
  N8: Part1.-, Componente2.GND#63
  N9: Part2.S, Componente2.GND#62
  N10: Part2.Vin, Componente2.5V#91
  N11: Part2.-, Componente2.D3/PWM0
  N12: Componente2.GND#50, COMPUTER_FAN1.BLACK

custom parts:
  Keyes Relay: The Keyes 5V relay module is suitable for SCM development, home appliance control. It uses a 5V~12V TIL control signal which can control DC / AC signal.
  KY-004 Key Switch Module: Arduino Key Switch Module Keyes KY-004 is a push button that will output a high signal when pressed.
  Arduino Nano (Rev3.0): Arduino Nano 3.0 IO expansion board
  Computer fan: This is a 5V computer fan
