# Fritzing sketch relay_example (saved by Fritzing 0.9.3b)

parts:
  Componente1 = Arduino Nano Expansion Board (Rev3.0)
  M1 = DC Motor
  VCC1 = Battery block 9V
  KY-1 = Keyes Relay [package=THT]
  Part1 = KY-004 Key Switch Module [package="Breakout board"]

nets:
  N1: Componente1.D2, Part1.S
  N2: Componente1.D3/PWM0, KY-1.signal
  N3: Componente1.GND#52, Part1.-
  N4: Componente1.GND#53, KY-1.ground
  N5: Componente1.GND#65, M1.pin_2
  N6: Componente1.5V#81, Part1.Vin
  N7: Componente1.5V#82, KY-1.power
  N8: M1.pin_1, KY-1.NC
  N9: VCC1.+, KY-1.C

custom parts:
  Arduino Nano Expansion Board (Rev3.0): Arduino Nano 3.0 IO expansion board
  Keyes Relay: The Keyes 5V relay module is suitable for SCM development, home appliance control. It uses a 5V~12V TIL control signal which can control DC / AC signal.
  KY-004 Key Switch Module: Arduino Key Switch Module Keyes KY-004 is a push button that will output a high signal when pressed.
