# Fritzing sketch relay_example_leonardo (saved by Fritzing 0.9.3b)

parts:
  M1 = DC Motor
  KY-1 = Keyes Relay [package=THT]
  Part1 = KY-004 Key Switch Module [package="Breakout board"]
  Leonardo_Shield1 = Arduino Leonardo with Arduino Sensor Shield v5

nets:
  N1: M1.pin_1, KY-1.NC
  N2: M1.pin_2, Leonardo_Shield1.GND#42
  N3: KY-1.signal, Leonardo_Shield1.D3
  N4: KY-1.power, Leonardo_Shield1.5V#46
  N5: KY-1.ground, Leonardo_Shield1.GND#23
  N6: KY-1.C, Leonardo_Shield1.5V#58
  N7: Part1.S, Leonardo_Shield1.D2
  N8: Part1.Vin, Leonardo_Shield1.5V#45
  N9: Part1.-, Leonardo_Shield1.GND#22

custom parts:
  Keyes Relay: The Keyes 5V relay module is suitable for SCM development, home appliance control. It uses a 5V~12V TIL control signal which can control DC / AC signal.
  KY-004 Key Switch Module: Arduino Key Switch Module Keyes KY-004 is a push button that will output a high signal when pressed.
  Arduino Leonardo with Arduino Sensor Shield v5: The D1 R32 is a mini wifi board based on the ESP32 with an Arduino Sensor Shield v5
