# Fritzing sketch relay_example_nano (saved by Fritzing 0.9.3b)

parts:
  M1 = DC Motor
  KY-1 = Keyes Relay [package=THT]
  Part1 = KY-004 Key Switch Module [package="Breakout board"]
  Componente1 = Arduino Nano (Rev3.0)

nets:
  N1: M1.pin_1, KY-1.NC
  N2: M1.pin_2, Componente1.GND#50
  N3: KY-1.signal, Componente1.D3/PWM0
  N4: KY-1.power, Componente1.5V#91
  N5: KY-1.ground, Componente1.GND#62
  N6: KY-1.C, Componente1.5V#79
  N7: Part1.S, Componente1.D2
  N8: Part1.Vin, Componente1.5V#92
  N9: Part1.-, Componente1.GND#63

custom parts:
  Keyes Relay: The Keyes 5V relay module is suitable for SCM development, home appliance control. It uses a 5V~12V TIL control signal which can control DC / AC signal.
  KY-004 Key Switch Module: Arduino Key Switch Module Keyes KY-004 is a push button that will output a high signal when pressed.
  Arduino Nano (Rev3.0): Arduino Nano 3.0 IO expansion board
