# Fritzing sketch relay_example_nodemcu (saved by Fritzing 0.9.3b)

parts:
  M1 = DC Motor
  KY-1 = Keyes Relay [package=THT]
  Part1 = KY-004 Key Switch Module [package="Breakout board"]
  Componente1 = NodeMcu base board

nets:
  N1: M1.pin_1, KY-1.NC
  N2: M1.pin_2, Componente1.G, Componente1.GND#52
  N3: KY-1.signal, Componente1.D3
  N4: KY-1.power, Part1.Vin, Componente1.3V
  N5: KY-1.ground, Part1.-, Componente1.GND#44, Componente1.GND#46
  N6: KY-1.C, Componente1.VU, Componente1.VUSB
  N7: Part1.S, Componente1.D2

custom parts:
  Keyes Relay: The Keyes 5V relay module is suitable for SCM development, home appliance control. It uses a 5V~12V TIL control signal which can control DC / AC signal.
  KY-004 Key Switch Module: Arduino Key Switch Module Keyes KY-004 is a push button that will output a high signal when pressed.
  NodeMcu base board: ESP8266 WiFi Expansion Board For NodeMCU ESP-12E
