# Fritzing sketch s12sd_example_leonardo (saved by Fritzing 0.9.3b)

parts:
  Leonardo_Shield2 = Arduino Leonardo with Arduino Sensor Shield v5
  Componente4 = GUVA-S12SD UV Light Sensor

nets:
  N1: Leonardo_Shield2.A0, Componente4.Out
  GND: Leonardo_Shield2.GND, Componente4.GND
  5V: Leonardo_Shield2.5V, Componente4.5V

custom parts:
  Arduino Leonardo with Arduino Sensor Shield v5: The D1 R32 is a mini wifi board based on the ESP32 with an Arduino Sensor Shield v5
  GUVA-S12SD UV Light Sensor: Extend your light-sensing spectrum with this analog UV sensor module. It uses a UV photodiode, which can detect the 240-370nm range of light (which covers UVB and most of UVA spectrum). The signal level from the photodiode is very small, in the nano-ampere level, so we tossed on an opamp to amplify the signal to a more manageable volt-level.
