# Fritzing sketch s12sd_example_nano (saved by Fritzing 0.9.3b)

parts:
  Componente3 = GUVA-S12SD UV Light Sensor
  Componente5 = Arduino Nano (Rev3.0)

nets:
  5V: Componente3.5V, Componente5.5V
  N1: Componente3.Out, Componente5.A0
  GND: Componente3.GND, Componente5.GND

custom parts:
  GUVA-S12SD UV Light Sensor: Extend your light-sensing spectrum with this analog UV sensor module. It uses a UV photodiode, which can detect the 240-370nm range of light (which covers UVB and most of UVA spectrum). The signal level from the photodiode is very small, in the nano-ampere level, so we tossed on an opamp to amplify the signal to a more manageable volt-level.
  Arduino Nano (Rev3.0): Arduino Nano 3.0 IO expansion board
