# Fritzing sketch s12sd_example_nodemcu (saved by Fritzing 0.9.3b)

parts:
  Componente3 = GUVA-S12SD UV Light Sensor
  Componente4 = NodeMcu base board

nets:
  N1: Componente3.5V, Componente4.3V
  N2: Componente3.Out, Componente4.A0
  GND: Componente3.GND, Componente4.GND

custom parts:
  GUVA-S12SD UV Light Sensor: Extend your light-sensing spectrum with this analog UV sensor module. It uses a UV photodiode, which can detect the 240-370nm range of light (which covers UVB and most of UVA spectrum). The signal level from the photodiode is very small, in the nano-ampere level, so we tossed on an opamp to amplify the signal to a more manageable volt-level.
  NodeMcu base board: ESP8266 WiFi Expansion Board For NodeMCU ESP-12E
