# Fritzing sketch s12sd_example_wemosD1R32 (saved by Fritzing 0.9.3b)

parts:
  Componente3 = GUVA-S12SD UV Light Sensor
  WeMos_D1_R32_Shield1 = WeMos D1 R32 with Arduino Sensor Shield v5

nets:
  5V: Componente3.5V, WeMos_D1_R32_Shield1.5V
  N1: Componente3.Out, WeMos_D1_R32_Shield1.A0
  GND: Componente3.GND, WeMos_D1_R32_Shield1.GND

custom parts:
  GUVA-S12SD UV Light Sensor: Extend your light-sensing spectrum with this analog UV sensor module. It uses a UV photodiode, which can detect the 240-370nm range of light (which covers UVB and most of UVA spectrum). The signal level from the photodiode is very small, in the nano-ampere level, so we tossed on an opamp to amplify the signal to a more manageable volt-level.
  WeMos D1 R32 with Arduino Sensor Shield v5: The D1 R32 is a mini wifi board based on the ESP32 with an Arduino Sensor Shield v5
