# Fritzing sketch servos360_example (saved by Fritzing 0.9.3b)

parts:
  Parte1 = Arduino Nano (Rev3.0)  # not connected
  Parte5 = Servo 3 Wire
  Parte6 = Servo 3 Wire
  R1 = Servo 360º [package=THT]
  R2 = Servo 360º [package=THT]  # not connected
  Parte7 = Servo 3 Wire
  Parte8 = Servo 3 Wire

nets:
  N1: Parte5.WIRE, Parte6.WIRE
  N2: Parte5.V, R1.+
  N3: Parte5.G, R1.S
  N4: Parte5.S, R1.-
  N5: Parte7.WIRE, Parte8.WIRE

custom parts:
  Arduino Nano (Rev3.0): Arduino Nano 3.0 IO expansion board
  Servo 3 Wire: Represents a servo 3 wire, make a connection with a black wire on the "WIRE" pin.
  Servo 360º: A continuous rotation servo
