# Fritzing sketch servos_example (saved by Fritzing 0.9.3b)

parts:
  Parte1 = Arduino Nano (Rev3.0)  # not connected
  J3 = Basic Servo
  Parte7 = Servo 3 Wire
  Parte8 = Servo 3 Wire
  J4 = Basic Servo
  Parte9 = Servo 3 Wire
  Parte10 = Servo 3 Wire

nets:
  N1: J3.gnd, Parte7.S
  N2: J3.vcc, Parte7.V
  N3: J3.pulse, Parte7.G
  N4: Parte7.WIRE, Parte8.WIRE
  N5: J4.gnd, Parte9.S
  N6: J4.vcc, Parte9.V
  N7: J4.pulse, Parte9.G
  N8: Parte9.WIRE, Parte10.WIRE

custom parts:
  Arduino Nano (Rev3.0): Arduino Nano 3.0 IO expansion board
  Servo 3 Wire: Represents a servo 3 wire, make a connection with a black wire on the "WIRE" pin.
