# Fritzing sketch sonar (saved by Fritzing 0.9.3b)

parts:
  Parte1 = Arduino Nano (Rev3.0)
  Parte12 = SRF05 Ultrasonic Rangefinder

nets:
  N1: Parte1.D7, Parte12.Echo
  GND: Parte1.D11/PWM5, Parte1.GND, Parte12.GND
  N2: Parte1.D13, Parte12.Trig
  5V: Parte1.5V, Parte12.VCC

custom parts:
  Arduino Nano (Rev3.0): Arduino Nano 3.0 IO expansion board
