# Fritzing sketch sonar_motors_example (saved by Fritzing 0.9.3b)

parts:
  Parte1 = Arduino Nano (Rev3.0)
  Parte5 = Servo 3 Wire
  Parte6 = Servo 3 Wire
  R1 = Servo 360º [package=THT]
  R2 = Servo 360º [package=THT]  # not connected
  Parte7 = Servo 3 Wire
  Parte8 = Servo 3 Wire
  hc-sr1 = hc-sr04

nets:
  N1: Parte1.D7, hc-sr1.Echo
  N2: Parte1.D11/PWM5, Parte1.GND#58, hc-sr1.GND
  N3: Parte1.D13, Parte1.GND#57, hc-sr1.Trig
  5V: Parte1.5V, hc-sr1.VCC
  N4: Parte5.WIRE, Parte6.WIRE
  N5: Parte5.V, R1.+
  N6: Parte5.G, R1.S
  N7: Parte5.S, R1.-
  N8: Parte7.WIRE, Parte8.WIRE

custom parts:
  Arduino Nano (Rev3.0): Arduino Nano 3.0 IO expansion board
  Servo 3 Wire: Represents a servo 3 wire, make a connection with a black wire on the "WIRE" pin.
  Servo 360º: A continuous rotation servo
  hc-sr04: This is a HC-SR04 Distance Sensor (based on HC-SR04 Fritzing Project)
