# Fritzing sketch robot_stepper_example (saved by Fritzing 0.9.3b)

parts:
  Componente1 = Arduino Nano Expansion Board (Rev3.0)
  X1 = X113647 Stepper Driver Board [package=board]
  MOTOR1 = 28BYJ-48 Stepper Motor
  X2 = X113647 Stepper Driver Board [package=board]
  MOTOR2 = 28BYJ-48 Stepper Motor

nets:
  N1: Componente1.D2, X1.IN1
  N2: Componente1.D3/PWM0, X1.IN3
  N3: Componente1.D4, X1.IN2
  N4: Componente1.D5/PWM1, X1.IN4
  N5: Componente1.D6/PWM2, X2.IN1
  N6: Componente1.D7, X2.IN3
  N7: Componente1.D8, X2.IN2
  N8: Componente1.D9/PWM3, X2.IN4
  GND: Componente1.GND, X1.GND
  N9: Componente1.5V, X1.+V
  N10: X1.BLUE, MOTOR1.BLUE
  N11: X1.PINK, MOTOR1.PINK
  N12: X1.YELLOW, MOTOR1.YELLOW
  N13: X1.ORANGE, MOTOR1.ORANGE
  N14: X1.RED, MOTOR1.RED
  N15: X2.BLUE, MOTOR2.BLUE
  N16: X2.PINK, MOTOR2.PINK
  N17: X2.YELLOW, MOTOR2.YELLOW
  N18: X2.ORANGE, MOTOR2.ORANGE
  N19: X2.RED, MOTOR2.RED

custom parts:
  Arduino Nano Expansion Board (Rev3.0): Arduino Nano 3.0 IO expansion board
  X113647 Stepper Driver Board: A common stepper motor driver board based on ULN2003APG darlington array
  28BYJ-48 Stepper Motor: 28BYJ-48 gear-reduction stepper motor (small)
