# Fritzing sketch stepper_example (saved by Fritzing 0.9.3b)

parts:
  Componente1 = Arduino Nano Expansion Board (Rev3.0)
  X1 = X113647 Stepper Driver Board [package=board]
  MOTOR1 = 28BYJ-48 Stepper Motor

nets:
  N1: Componente1.D2, X1.IN1
  N2: Componente1.D3/PWM0, X1.IN3
  N3: Componente1.D4, X1.IN2
  N4: Componente1.D5/PWM1, X1.IN4
  GND: Componente1.GND, X1.GND
  N5: Componente1.5V, X1.+V
  N6: X1.BLUE, MOTOR1.BLUE
  N7: X1.PINK, MOTOR1.PINK
  N8: X1.YELLOW, MOTOR1.YELLOW
  N9: X1.ORANGE, MOTOR1.ORANGE
  N10: X1.RED, MOTOR1.RED

custom parts:
  Arduino Nano Expansion Board (Rev3.0): Arduino Nano 3.0 IO expansion board
  X113647 Stepper Driver Board: A common stepper motor driver board based on ULN2003APG darlington array
  28BYJ-48 Stepper Motor: 28BYJ-48 gear-reduction stepper motor (small)
