# Fritzing sketch push_button (saved by Fritzing 0.9.3b)

parts:
  Parte1 = Arduino Nano (Rev3.0)
  VCC3 = Battery block 9V  # not connected
  S7 = Piezo-electric buzzer

nets:
  N1: Parte1.D3/PWM0, S7.Signal
  GND: Parte1.GND, S7.Gnd
  5V: Parte1.5V, S7.Vcc

custom parts:
  Arduino Nano (Rev3.0): Arduino Nano 3.0 IO expansion board
  Piezo-electric buzzer: Piezo-electric buzzer (speaker)
