# Fritzing sketch switch_example (saved by Fritzing 0.9.3b)
breadboards: 1

parts:
  Componente1 = Arduino Nano Expansion Board (Rev3.0)
  S1 = Pushbutton [package="[THT]"]
  R2 = Resistor [tolerance=±5% resistance=10k package="2512 [SMD]"]

nets:
  N1: Componente1.D2, S1.Pin_3, S1.Pin_4, R2.Pin_1
  N2: Componente1.GND, S1.Pin_1, S1.Pin_2
  N3: Componente1.5V, R2.Pin_0

custom parts:
  Arduino Nano Expansion Board (Rev3.0): Arduino Nano 3.0 IO expansion board
