# Fritzing sketch switch_led_example (saved by Fritzing 0.9.3b)
breadboards: 1

parts:
  Componente1 = Arduino Nano Expansion Board (Rev3.0)
  S1 = Pushbutton [package="[THT]"]
  R2 = Resistor [tolerance=±5% resistance=220 package="2512 [SMD]"]
  R3 = Resistor [tolerance=±5% resistance=220 package="2512 [SMD]"]
  LED1 = LED - 5mm [color="Red (633nm)" package="5 mm [THT]"]

nets:
  N1: Componente1.D2, R2.Pin_0
  N2: Componente1.GND, S1.Pin_1, S1.Pin_2
  N3: Componente1.5V, R3.Pin_0
  N4: S1.Pin_3, S1.Pin_4, R2.Pin_1, LED1.cathode
  N5: R3.Pin_1, LED1.anode

custom parts:
  Arduino Nano Expansion Board (Rev3.0): Arduino Nano 3.0 IO expansion board
