# Fritzing sketch switches_example (saved by Fritzing 0.9.3b)
breadboards: 1

parts:
  Componente1 = Arduino Nano Expansion Board (Rev3.0)
  S1 = Pushbutton [package="[THT]"]
  R2 = Resistor [tolerance=±5% resistance=220 package="2512 [SMD]"]
  S2 = Pushbutton [package="[THT]"]
  R3 = Resistor [tolerance=±5% resistance=220 package="2512 [SMD]"]

nets:
  N1: Componente1.D10/PWM4, S1.Pin_3, S1.Pin_4, R2.Pin_1
  N2: Componente1.D11/PWM5, S2.Pin_3, S2.Pin_4, R3.Pin_1
  N3: Componente1.GND, S1.Pin_1, S1.Pin_2, S2.Pin_1, S2.Pin_2
  N4: Componente1.5V, R2.Pin_0, R3.Pin_0

custom parts:
  Arduino Nano Expansion Board (Rev3.0): Arduino Nano 3.0 IO expansion board
