# Fritzing sketch switches_example_leonardo (saved by Fritzing 0.9.3b)

parts:
  Part1 = KY-004 Key Switch Module [package="Breakout board"]
  Part2 = KY-004 Key Switch Module [package="Breakout board"]
  Leonardo_Shield1 = Arduino Leonardo with Arduino Sensor Shield v5

nets:
  N1: Part1.S, Leonardo_Shield1.D3
  N2: Part1.Vin, Leonardo_Shield1.5V#46
  N3: Part1.-, Leonardo_Shield1.GND#23
  N4: Part2.S, Leonardo_Shield1.D2
  N5: Part2.Vin, Leonardo_Shield1.5V#45
  N6: Part2.-, Leonardo_Shield1.GND#22

custom parts:
  KY-004 Key Switch Module: Arduino Key Switch Module Keyes KY-004 is a push button that will output a high signal when pressed.
  Arduino Leonardo with Arduino Sensor Shield v5: The D1 R32 is a mini wifi board based on the ESP32 with an Arduino Sensor Shield v5
