# Fritzing sketch switches_example_nano (saved by Fritzing 0.9.3b)

parts:
  Part1 = KY-004 Key Switch Module [package="Breakout board"]
  Part2 = KY-004 Key Switch Module [package="Breakout board"]
  Componente1 = Arduino Nano (Rev3.0)

nets:
  N1: Part1.S, Componente1.D3/PWM0
  N2: Part1.Vin, Componente1.5V#91
  N3: Part1.-, Componente1.GND#62
  N4: Part2.S, Componente1.D2
  N5: Part2.Vin, Componente1.5V#92
  N6: Part2.-, Componente1.GND#63

custom parts:
  KY-004 Key Switch Module: Arduino Key Switch Module Keyes KY-004 is a push button that will output a high signal when pressed.
  Arduino Nano (Rev3.0): Arduino Nano 3.0 IO expansion board
