# Fritzing sketch switches_example_nodemcu (saved by Fritzing 0.9.3b)

parts:
  Part1 = KY-004 Key Switch Module [package="Breakout board"]
  Part2 = KY-004 Key Switch Module [package="Breakout board"]
  Componente1 = NodeMcu base board

nets:
  N1: Part1.S, Componente1.D3
  VIN: Part1.Vin, Part2.Vin, Componente1.3V
  N2: Part1.-, Part2.-, Componente1.GND
  N3: Part2.S, Componente1.D2

custom parts:
  KY-004 Key Switch Module: Arduino Key Switch Module Keyes KY-004 is a push button that will output a high signal when pressed.
  NodeMcu base board: ESP8266 WiFi Expansion Board For NodeMCU ESP-12E
