# Fritzing sketch TCRT5000 (saved by Fritzing 0.9.3b)

parts:
  Parte1 = Arduino Nano (Rev3.0)
  U2 = TCRT5000 Line Tracker

nets:
  N1: Parte1.A4, U2.Do
  N2: Parte1.A0, U2.Ao

custom parts:
  Arduino Nano (Rev3.0): Arduino Nano 3.0 IO expansion board
  TCRT5000 Line Tracker: A line tracker module based on TCRT5000 (Vishay)
