# Fritzing sketch tcs3200_example (saved by Fritzing 0.9.3b)

parts:
  Parte1 = Arduino Nano (Rev3.0)
  C1 = Color Sensor TCS320

nets:
  N1: Parte1.D2, Parte1.D3/PWM0, C1.S0, C1.S1
  N2: Parte1.D4, Parte1.D5/PWM1, C1.S2, C1.S3
  N3: Parte1.D6/PWM2, C1.Out
  GND: Parte1.GND, C1.Gnd
  5V: Parte1.5V, C1.Vcc

custom parts:
  Arduino Nano (Rev3.0): Arduino Nano 3.0 IO expansion board
