# Fritzing sketch semaphore_leds (saved by Fritzing 0.9.3b)
breadboards: 1

parts:
  LED1 = smd LED [color="Red (635nm)" package="0603 [SMD]"]
  LED2 = smd LED [color="Yellow (592nm)" package="0603 [SMD]"]
  LED3 = smd LED [color="Green (555nm)" package="0603 [SMD]"]
  LED4 = smd LED [color="Red (635nm)" package="0603 [SMD]"]
  LED5 = smd LED [color="Yellow (592nm)" package="0603 [SMD]"]
  LED6 = smd LED [color="Green (555nm)" package="0603 [SMD]"]
  R1 = Resistor [tolerance=±5% resistance=1k package="1206 [SMD]"]
  Componente1 = Arduino Nano (Rev3.0)
  R2 = Resistor [tolerance=±5% resistance=1k package="1206 [SMD]"]
  R3 = Resistor [tolerance=±5% resistance=1k package="1206 [SMD]"]
  R4 = Resistor [tolerance=±5% resistance=1k package="1206 [SMD]"]
  R5 = Resistor [tolerance=±5% resistance=1k package="1206 [SMD]"]
  R6 = Resistor [tolerance=±5% resistance=1k package="1206 [SMD]"]

nets:
  N1: LED1.cathode, LED2.cathode, LED3.cathode, LED4.cathode, LED5.cathode, LED6.cathode, Componente1.GND
  N2: LED1.anode, R1.Pin_0
  N3: LED2.anode, R2.Pin_0
  N4: LED3.anode, R3.Pin_0
  N5: LED4.anode, R4.Pin_0
  N6: LED5.anode, R5.Pin_0
  N7: LED6.anode, R6.Pin_0
  N8: R1.Pin_1, Componente1.D2
  N9: Componente1.D3/PWM0, R2.Pin_1
  N10: Componente1.D4, R3.Pin_1
  N11: Componente1.D5/PWM1, R4.Pin_1
  N12: Componente1.D6/PWM2, R5.Pin_1
  N13: Componente1.D7, R6.Pin_1

custom parts:
  Arduino Nano (Rev3.0): Arduino Nano 3.0 IO expansion board
