# Fritzing sketch wemos_D1R32_LEDs (saved by Fritzing 0.9.3b)
breadboards: 1

parts:
  WeMos_D1_R1 = WeMos D1 R32
  R1 = Resistor [tolerance=±5% resistance=220 package="0805 [SMD]"]
  LED1 = LED - 3mm [color="Blue (430nm)" package="3 mm [THT]"]
  LED2 = LED - 3mm [color="Red (633nm)" package="3 mm [THT]"]
  R2 = Resistor [tolerance=±5% resistance=220 package="0805 [SMD]"]

nets:
  N1: WeMos_D1_R1.IO19, R2.Pin_0
  N2: WeMos_D1_R1.IO18, R1.Pin_0
  N3: WeMos_D1_R1.GND, LED1.cathode, LED2.cathode
  N4: R1.Pin_1, LED1.anode
  N5: LED2.anode, R2.Pin_1

custom parts:
  WeMos D1 R32: The D1 R32 is a mini wifi board based on the ESP32.
