# Fritzing sketch uno_LEDs_servo_relay (saved by Fritzing 0.9.3b)
breadboards: 1

parts:
  R9 = Resistor [tolerance=±5% resistance=3.3k package="1206 [SMD]"]
  R10 = Resistor [tolerance=±5% resistance=3.3k package="1206 [SMD]"]
  LED1_D14 = smd LED [color="Blue (430nm)" package="0805 [SMD]"]
  LED2_D13 = smd LED [color="Red (633nm)" package="0805 [SMD]"]
  Componente1 = Arduino Uno (Rev3)
  J2 = Basic Servo
  KY-2 = Keyes Relay [package=THT]
  COMPUTER_FAN2 = Computer fan
  Componente2 = Bluetooth HC-05 Macho

nets:
  N1: R9.Pin_0, Componente1.D12/MISO
  N2: R9.Pin_1, LED2_D13.anode
  N3: R10.Pin_0, Componente1.D13/SCK
  N4: R10.Pin_1, LED1_D14.anode
  GND: LED1_D14.cathode, LED2_D13.cathode, Componente1.GND, J2.gnd, KY-2.ground, COMPUTER_FAN2.BLACK, Componente2.GND
  N5: Componente1.D11_PWM/MOSI, J2.pulse
  N6: Componente1.D2, Componente2.TXD
  N7: Componente1.D3_PWM, Componente2.RXD
  N8: Componente1.D7, KY-2.signal
  VCC: Componente1.5V, J2.vcc, KY-2.power, KY-2.C, Componente2.VCC
  N9: KY-2.NO, COMPUTER_FAN2.RED

custom parts:
  Keyes Relay: The Keyes 5V relay module is suitable for SCM development, home appliance control. It uses a 5V~12V TIL control signal which can control DC / AC signal.
  Computer fan: This is a 5V computer fan
