# Fritzing sketch uno_bluetooth (saved by Fritzing 0.9.3b)

parts:
  Componente1 = Arduino Uno (Rev3)
  Componente2 = Bluetooth HC-05 Macho

nets:
  GND: Componente1.GND, Componente2.GND
  N1: Componente1.D2, Componente2.TXD
  N2: Componente1.D3_PWM, Componente2.RXD
