# Fritzing sketch ws2812_3leds_leonardo (saved by Fritzing 0.9.3b)

parts:
  Componente1 = ws2812b [package="smd 2812b"]
  Componente2 = ws2812b [package="smd 2812b"]
  Componente3 = ws2812b [package="smd 2812b"]
  Componente4 = Arduino Leonardo (Rev3b)

nets:
  VDD: Componente1.VDD, Componente2.VDD, Componente3.VDD, Componente4.3V3
  N1: Componente1.DOUT, Componente3.DIN
  VSS: Componente1.VSS, Componente2.VSS, Componente3.VSS, Componente4.GND
  N2: Componente1.DIN, Componente2.DOUT
  N3: Componente2.DIN, Componente4.D2/SDA
