# Fritzing sketch ws2812_3leds_nano (saved by Fritzing 0.9.3b)

parts:
  Componente1 = ws2812b [package="smd 2812b"]
  Componente2 = ws2812b [package="smd 2812b"]
  Componente3 = ws2812b [package="smd 2812b"]
  Componente6 = Arduino Nano Expansion Board (Rev3.0)

nets:
  VDD: Componente1.VDD, Componente2.VDD, Componente3.VDD, Componente6.5V
  N1: Componente1.DOUT, Componente3.DIN
  VSS: Componente1.VSS, Componente2.VSS, Componente3.VSS, Componente6.GND
  N2: Componente1.DIN, Componente2.DOUT
  N3: Componente2.DIN, Componente6.D2

custom parts:
  Arduino Nano Expansion Board (Rev3.0): Arduino Nano 3.0 IO expansion board
