# Fritzing sketch ws2812_3leds_nodemcu (saved by Fritzing 0.9.3b)

parts:
  Componente1 = ws2812b [package="smd 2812b"]
  Componente2 = ws2812b [package="smd 2812b"]
  Componente3 = ws2812b [package="smd 2812b"]
  Componente5 = ESP12E Motor Shield

nets:
  VDD: Componente1.VDD, Componente2.VDD, Componente3.VDD, Componente5.3V
  N1: Componente1.DOUT, Componente3.DIN
  VSS: Componente1.VSS, Componente2.VSS, Componente3.VSS, Componente5.GND
  N2: Componente1.DIN, Componente2.DOUT
  N3: Componente2.DIN, Componente5.D2

custom parts:
  ESP12E Motor Shield: ESP8266 WiFi Motor Drive Expansion Board For NodeMCU ESP-12E
