# Fritzing sketch ws2812_3leds_wemosD1R32 (saved by Fritzing 0.9.3b)

parts:
  WeMos_D1_R1 = WeMos D1 R32
  Componente1 = ws2812b [package="smd 2812b"]
  Componente2 = ws2812b [package="smd 2812b"]
  Componente3 = ws2812b [package="smd 2812b"]

nets:
  N1: WeMos_D1_R1.IO26, Componente2.DIN
  VSS: WeMos_D1_R1.GND, Componente1.VSS, Componente2.VSS, Componente3.VSS
  VDD: WeMos_D1_R1.3.3V, Componente1.VDD, Componente2.VDD, Componente3.VDD
  N2: Componente1.DOUT, Componente3.DIN
  N3: Componente1.DIN, Componente2.DOUT

custom parts:
  WeMos D1 R32: The D1 R32 is a mini wifi board based on the ESP32.
