# Fritzing sketch ws2812_example (saved by Fritzing 0.9.3b)

parts:
  Componente1 = Arduino Nano Expansion Board (Rev3.0)
  R2 = Photocell (LDR) [package=THT]

nets:
  N1: Componente1.D2, R2.OUT
  GND: Componente1.GND, R2.GND
  5V: Componente1.5V, R2.VCC

custom parts:
  Arduino Nano Expansion Board (Rev3.0): Arduino Nano 3.0 IO expansion board
  Photocell (LDR): A generic light dependent resistor (LDR)
