# Fritzing sketch ws2812_leonardo (saved by Fritzing 0.9.3b)

parts:
  R2 = Photocell (LDR) [package=THT]
  Componente2 = Arduino Leonardo (Rev3b)

nets:
  N1: R2.OUT, Componente2.D2/SDA
  VCC: R2.VCC, Componente2.3V3
  GND: R2.GND, Componente2.GND

custom parts:
  Photocell (LDR): A generic light dependent resistor (LDR)
