# Fritzing sketch ws2812_nodemcu (saved by Fritzing 0.9.3b)

parts:
  R2 = Photocell (LDR) [package=THT]
  Componente2 = ESP12E Motor Shield

nets:
  N1: R2.OUT, Componente2.D2
  N2: R2.VCC, Componente2.3V
  GND: R2.GND, Componente2.GND

custom parts:
  Photocell (LDR): A generic light dependent resistor (LDR)
  ESP12E Motor Shield: ESP8266 WiFi Motor Drive Expansion Board For NodeMCU ESP-12E
