# Fritzing sketch ws2812_wemosD1R32 (saved by Fritzing 0.9.3b)

parts:
  R2 = Photocell (LDR) [package=THT]
  WeMos_D1_R1 = WeMos D1 R32

nets:
  N1: R2.OUT, WeMos_D1_R1.IO26
  VCC: R2.VCC, WeMos_D1_R1.3.3V
  GND: R2.GND, WeMos_D1_R1.GND

custom parts:
  Photocell (LDR): A generic light dependent resistor (LDR)
  WeMos D1 R32: The D1 R32 is a mini wifi board based on the ESP32.
