# Fritzing sketch ws2812b_board (saved by Fritzing 0.9.3b)
circuit board: 2.77512cm x 2.7789cm

parts:
  OUT = Dagu DGServo 9g header (male) [package=THT]
  IN = Dagu DGServo 9g header (male) [package=THT]
  U1 = ws2812b [package="smd 2812b"]
  U5 = ws2812b [package="smd 2812b"]
  U3 = ws2812b [package="smd 2812b"]
  U7 = ws2812b [package="smd 2812b"]
  U6 = ws2812b [package="smd 2812b"]
  U2 = ws2812b [package="smd 2812b"]
  U4 = ws2812b [package="smd 2812b"]
  C1 = Capacitor [package=0805]
  C7 = Capacitor [package=0805]
  C6 = Capacitor [package=0805]
  C5 = Capacitor [package=0805]
  C4 = Capacitor [package=0805]
  C3 = Capacitor [package=0805]
  C2 = Capacitor [package=0805]

nets:
  VSS: OUT.gnd, IN.gnd, U1.VSS, U5.VSS, U3.VSS, U7.VSS, U6.VSS, U2.VSS, U4.VSS, C1.2, C7.2, C6.2, C5.2, C4.2, C3.2, C2.2
  VDD: OUT.Vcc, IN.Vcc, U1.VDD, U5.VDD, U3.VDD, U7.VDD, U6.VDD, U2.VDD, U4.VDD, C1.1, C7.1, C6.1, C5.1, C4.1, C3.1, C2.1
  N1: OUT.pulse, U7.DOUT
  N2: IN.pulse, U1.DIN
  N3: U1.DOUT, U2.DIN
  N4: U5.DOUT, U6.DIN
  N5: U5.DIN, U4.DOUT
  N6: U3.DOUT, U4.DIN
  N7: U3.DIN, U2.DOUT
  N8: U7.DIN, U6.DOUT
